// Logisim project WordTTY.circ as structural Verilog: 1 circuit, main circuit main
module main (
  input  [6:0] char1,
  input  [6:0] char2,
  input  [6:0] char3,
  input  [6:0] char4,
  input  [6:0] char5,
  input  [6:0] char6,
  input  [6:0] char7,
  input  reset,
  input  [6:0] char8,
  input  clock,
  input  print,
  output [6:0] char
);

  wire [3:0] counter_1_q;
  wire [6:0] char1_q, char2_q, char3_q, char4_q, char5_q, char6_q, char7_q, char8_q, char_space_q;

  Register #(.width(7)) char_space (.D({7{1'b0}}), .Q(char_space_q), .clk(clock));  // open: en, clr
  Register #(.width(7)) u_char1 (.D(char1), .Q(char1_q), .clk(clock));  // open: en, clr
  Register #(.width(7)) u_char2 (.D(char2), .Q(char2_q), .clk(clock));  // open: en, clr
  Register #(.width(7)) u_char3 (.D(char3), .Q(char3_q), .clk(clock));  // open: en, clr
  Register #(.width(7)) u_char4 (.D(char4), .Q(char4_q), .clk(clock));  // open: en, clr
  Register #(.width(7)) u_char5 (.D(char5), .Q(char5_q), .clk(clock));  // open: en, clr
  Register #(.width(7)) u_char6 (.D(char6), .Q(char6_q), .clk(clock));  // open: en, clr
  Register #(.width(7)) u_char7 (.D(char7), .Q(char7_q), .clk(clock));  // open: en, clr
  Register #(.width(7)) u_char8 (.D(char8), .Q(char8_q), .clk(clock));  // open: en, clr
  Multiplexer #(.select(4), .width(7), .enable("false")) multiplexer_1 (
    .in0(char_space_q), .in1(char1_q), .in2(char2_q), .in3(char3_q), .in4(char4_q), .in5(char5_q),
    .in6(char6_q), .in7(char7_q), .in8(char8_q), .out(char), .sel(counter_1_q));  // open: in9, in10, in11, in12, in13, in14, in15
  Counter #(.width(4), .max('hf)) counter_1 (
    .count(print), .Q(counter_1_q), .clk(clock), .clr(reset));  // open: load, D, carry
endmodule
