// Logisim project board.circ as structural Verilog: 1 circuit, main circuit main
module main (
  input  a,
  input  b,
  input  c,
  input  d,
  input  e,
  input  f,
  input  g,
  input  h,
  input  i,
  input  j,
  input  k,
  input  l,
  input  m,
  input  n,
  input  o,
  input  p,
  output [6:0] char
);

  wire [3:0] priority_encoder_1_out;

  Priority_Encoder #(.select(4)) priority_encoder_1 (
    .in0(a), .in1(b), .in2(c), .in3(d), .in4(e), .in5(f), .in6(g), .in7(h), .in8(i), .in9(j), .in10(k),
    .in11(l), .in12(m), .in13(n), .in14(o), .in15(p), .out(priority_encoder_1_out));  // open: gs, en_out, en_in
  Multiplexer #(.select(4), .width(7), .enable("false")) multiplexer_1 (
    .in0(7'b1100001), .in1(7'b1100010), .in2(7'b1100011), .in3(7'b1100100), .in4(7'b1100101),
    .in5(7'b1100110), .in6(7'b1100111), .in7(7'b1101000), .in8(7'b1101001), .in9(7'b1101010),
    .in10(7'b1101011), .in11(7'b1101100), .in12(7'b1101101), .in13(7'b1101110), .in14(7'b1101111),
    .in15(7'b1110000), .out(char), .sel(priority_encoder_1_out));
endmodule
