// Logisim project board2.circ as structural Verilog: 1 circuit, main circuit main
module main (
  input  q,
  input  r,
  input  s,
  input  t,
  input  u,
  input  v,
  input  w,
  input  x,
  input  y,
  input  z,
  output [6:0] char
);

  wire [3:0] priority_encoder_1_out;

  Priority_Encoder #(.select(4)) priority_encoder_1 (
    .in0(q), .in1(r), .in2(s), .in3(t), .in4(u), .in5(v), .in6(w), .in7(x), .in8(y), .in9(z),
    .out(priority_encoder_1_out));  // open: in10, in11, in12, in13, in14, in15, gs, en_out, en_in
  Multiplexer #(.select(4), .width(7), .enable("false")) multiplexer_1 (
    .in0(7'b1110001), .in1(7'b1110010), .in2(7'b1110011), .in3(7'b1110100), .in4(7'b1110101),
    .in5(7'b1110110), .in6(7'b1110111), .in7(7'b1111000), .in8(7'b1111001), .in9(7'b1111010), .out(char),
    .sel(priority_encoder_1_out));  // open: in10, in11, in12, in13, in14, in15
endmodule
