// Logisim project foundedTTYDataPath.circ as structural Verilog: 1 circuit, main circuit main
module main (
  input  [6:0] char1,
  input  [6:0] char2,
  input  [6:0] char3,
  input  [6:0] char4,
  input  [6:0] char5,
  input  [6:0] char6,
  input  [6:0] char7,
  input  [6:0] char8,
  input  [6:0] founded,
  input  clock,
  output [6:0] char
);

  wire comparator_1_eq, comparator_2_eq, comparator_3_eq, comparator_4_eq, comparator_5_eq, comparator_6_eq,
       comparator_7_eq, comparator_8_eq;
  wire [2:0] counter_1_q;
  wire [6:0] char1_q, char2_q, char3_q, char4_q, char5_q, char6_q, char7_q, char8_q, multiplexer_1_out,
       multiplexer_2_out, multiplexer_3_out, multiplexer_4_out, multiplexer_5_out, multiplexer_6_out,
       multiplexer_7_out, multiplexer_8_out;

  Comparator #(.width(7)) comparator_1 (.a(char1), .b(founded), .eq(comparator_1_eq));  // open: gt, lt
  Comparator #(.width(7)) comparator_2 (.a(char2), .b(founded), .eq(comparator_2_eq));  // open: gt, lt
  Comparator #(.width(7)) comparator_3 (.a(char3), .b(founded), .eq(comparator_3_eq));  // open: gt, lt
  Comparator #(.width(7)) comparator_4 (.a(char4), .b(founded), .eq(comparator_4_eq));  // open: gt, lt
  Comparator #(.width(7)) comparator_5 (.a(char5), .b(founded), .eq(comparator_5_eq));  // open: gt, lt
  Comparator #(.width(7)) comparator_6 (.a(char6), .b(founded), .eq(comparator_6_eq));  // open: gt, lt
  Comparator #(.width(7)) comparator_7 (.a(char7), .b(founded), .eq(comparator_7_eq));  // open: gt, lt
  Comparator #(.width(7)) comparator_8 (.a(char8), .b(founded), .eq(comparator_8_eq));  // open: gt, lt
  Multiplexer #(.width(7), .enable("false")) multiplexer_1 (
    .in0(7'b0100000), .in1(founded), .out(multiplexer_1_out), .sel(comparator_1_eq));
  Multiplexer #(.width(7), .enable("false")) multiplexer_2 (
    .in0(7'b0100000), .in1(founded), .out(multiplexer_2_out), .sel(comparator_2_eq));
  Multiplexer #(.width(7), .enable("false")) multiplexer_3 (
    .in0(7'b0100000), .in1(founded), .out(multiplexer_3_out), .sel(comparator_3_eq));
  Multiplexer #(.width(7), .enable("false")) multiplexer_4 (
    .in0(7'b0100000), .in1(founded), .out(multiplexer_4_out), .sel(comparator_4_eq));
  Multiplexer #(.width(7), .enable("false")) multiplexer_5 (
    .in0(7'b0100000), .in1(founded), .out(multiplexer_5_out), .sel(comparator_5_eq));
  Multiplexer #(.width(7), .enable("false")) multiplexer_6 (
    .in0(7'b0100000), .in1(founded), .out(multiplexer_6_out), .sel(comparator_6_eq));
  Multiplexer #(.width(7), .enable("false")) multiplexer_7 (
    .in0(7'b0100000), .in1(founded), .out(multiplexer_7_out), .sel(comparator_7_eq));
  Multiplexer #(.width(7), .enable("false")) multiplexer_8 (
    .in0(7'b0100000), .in1(founded), .out(multiplexer_8_out), .sel(comparator_8_eq));
  Register #(.width(7)) u_char1 (.D(multiplexer_1_out), .Q(char1_q), .clk(clock));  // open: en, clr
  Register #(.width(7)) u_char2 (.D(multiplexer_2_out), .Q(char2_q), .clk(clock));  // open: en, clr
  Register #(.width(7)) u_char3 (.D(multiplexer_3_out), .Q(char3_q), .clk(clock));  // open: en, clr
  Register #(.width(7)) u_char4 (.D(multiplexer_4_out), .Q(char4_q), .clk(clock));  // open: en, clr
  Register #(.width(7)) u_char5 (.D(multiplexer_5_out), .Q(char5_q), .clk(clock));  // open: en, clr
  Register #(.width(7)) u_char6 (.D(multiplexer_6_out), .Q(char6_q), .clk(clock));  // open: en, clr
  Register #(.width(7)) u_char7 (.D(multiplexer_7_out), .Q(char7_q), .clk(clock));  // open: en, clr
  Register #(.width(7)) u_char8 (.D(multiplexer_8_out), .Q(char8_q), .clk(clock));  // open: en, clr
  Multiplexer #(.select(3), .width(7), .enable("false")) multiplexer_9 (
    .in0(char1_q), .in1(char2_q), .in2(char3_q), .in3(char4_q), .in4(char5_q), .in5(char6_q), .in6(char7_q),
    .in7(char8_q), .out(char), .sel(counter_1_q));
  Counter #(.width(3), .max('h7)) counter_1 (.Q(counter_1_q), .clk(clock));  // open: load, D, count, carry, clr
endmodule
