// Logisim project gameDataPath.circ as structural Verilog: 1 circuit, main circuit main
module main (
  input  CLOCK,
  input  a,
  input  lScoreUser,
  input  b,
  input  sScoreUser,
  input  c,
  input  d,
  input  lScorePC,
  input  e,
  input  sScorePC,
  input  f,
  input  g,
  input  lFalse,
  input  h,
  input  sFalse,
  input  i,
  input  j,
  input  k,
  input  lControlGame,
  input  l,
  input  scontrolGame,
  input  m,
  input  n,
  input  lcontInputWord,
  input  o,
  input  sconInputWord,
  input  lcharUser,
  input  p,
  input  q,
  input  r,
  input  s,
  input  [6:0] char,
  input  t,
  input  lchar,
  input  u,
  input  v,
  input  goInputWord,
  input  w,
  input  x,
  input  y,
  input  z,
  input  lsize,
  input  resetWordTTY,
  input  printWordTTY,
  output [3:0] scoreUser,
  output [3:0] scorePC,
  output [3:0] false,
  output [6:0] less,
  output falseEq,
  output falseLess,
  output [3:0] controlGame,
  output controlGAmeEq,
  output clockEqu,
  output clockLess,
  output [6:0] char1,
  output [6:0] char2,
  output [6:0] char3,
  output [6:0] char4,
  output [3:0] size,
  output [6:0] char5,
  output [6:0] char6,
  output includeTrue,
  output [6:0] char7,
  output [6:0] char8,
  output [6:0] ttyCharFound,
  output [13:0] man1,
  output [6:0] ttyCharword,
  output [13:0] man2,
  output [13:0] man3,
  output [13:0] man9,
  output [13:0] man4,
  output [13:0] man10,
  output [13:0] man5,
  output [13:0] man11,
  output [13:0] man6,
  output [13:0] man12,
  output [13:0] man7,
  output [13:0] man8
);

  wire main_1_l1, main_1_l2, main_1_l3, main_1_l4, main_1_l5, main_1_l6, main_1_l7, main_1_l8, main_3_lman1,
       main_3_lman2, main_3_lman3, main_3_lman4, main_3_lman5, main_3_lman6, main_3_lman7, main_3_lman8,
       main_3_lman9, main_3_lman10, main_3_lman11, main_3_lman12, main_3_sman2_3, main_4__0, main_4__1,
       main_4__2, main_4__3, main_4__4, main_4__5, main_4__6, main_4__7, main_4__8, main_4__9, main_4__10;
  wire [1:0] main_3_sman4, main_3_sman5_6, main_3_sman7, main_3_sman10, main_3_sman11;
  wire [2:0] main_3_sman8, main_3_sman9;
  wire [3:0] counter_1_q, counter_4_q, counter_5_q, false_q, main_2_size, multiplexer_1_out,
       multiplexer_2_out, multiplexer_3_out, multiplexer_4_out;
  wire [4:0] counter_3_q, InputWord_q, multiplexer_5_out;
  wire [6:0] main_2__1_char, main_2__2_char, main_2__3_char, main_2__4_char, main_2__5_char, main_2__6_char,
       main_2__7_char, main_2__8_char, register_10_q;

  Counter #(.width(4), .max('hf)) counter_1 (
    .D(scorePC), .count(sScorePC), .Q(counter_1_q), .clk(CLOCK));  // open: load, carry, clr
  inputWordFSM_main main_1 (
    .goInputWord(goInputWord), .clock(CLOCK), .l1(main_1_l1), .l2(main_1_l2), .l3(main_1_l3), .l4(main_1_l4),
    .l5(main_1_l5), .l6(main_1_l6), .l7(main_1_l7), .l8(main_1_l8));
  Multiplexer #(.width(4), .enable("false")) multiplexer_1 (
    .in0(4'b0000), .in1(counter_4_q), .out(multiplexer_1_out), .sel(sScoreUser));
  Multiplexer #(.width(4), .enable("false")) multiplexer_2 (
    .in0(4'b0000), .in1(counter_1_q), .out(multiplexer_2_out), .sel(sScorePC));
  Multiplexer #(.width(4), .enable("false")) multiplexer_3 (
    .in0(4'b0000), .in1(false), .out(multiplexer_3_out), .sel(sFalse));
  Multiplexer #(.width(4), .enable("false")) multiplexer_4 (
    .in0(4'b0000), .in1(counter_5_q), .out(multiplexer_4_out), .sel(scontrolGame));
  Multiplexer #(.width(5), .enable("false")) multiplexer_5 (
    .in0(5'b00001), .in1(counter_3_q), .out(multiplexer_5_out), .sel(sconInputWord));
  Register #(.width(4)) register_1 (.D(main_2_size), .en(lsize), .Q(size), .clk(CLOCK));  // open: clr
  Register #(.width(4)) u_scoreUser (.D(multiplexer_1_out), .en(lScoreUser), .Q(scoreUser), .clk(CLOCK));  // open: clr
  Register #(.width(4)) u_scorePC (.D(multiplexer_2_out), .en(lScorePC), .Q(scorePC), .clk(CLOCK));  // open: clr
  Register #(.width(4)) u_false (.D(multiplexer_3_out), .en(lFalse), .Q(false_q), .clk(CLOCK));  // open: clr
  Register #(.width(4)) u_controlGame (
    .D(multiplexer_4_out), .en(lControlGame), .Q(controlGame), .clk(CLOCK));  // open: clr
  Register #(.width(5)) InputWord (
    .D(multiplexer_5_out), .en(lcontInputWord), .Q(InputWord_q), .clk(CLOCK));  // open: clr
  inputWordDataPath_main main_2 (
    .l1(main_1_l1), .l2(main_1_l2), .l3(main_1_l3), .inputChar(char), .l4(main_1_l4), .l5(main_1_l5),
    .l6(main_1_l6), .l7(main_1_l7), .l8(main_1_l8), ._1_char(main_2__1_char), ._2_char(main_2__2_char),
    ._3_char(main_2__3_char), .size(main_2_size), ._4_char(main_2__4_char), ._5_char(main_2__5_char),
    ._6_char(main_2__6_char), ._7_char(main_2__7_char), ._8_char(main_2__8_char), .clock(CLOCK));  // open: less
  hangmanPrintFSM_main main_3 (
    ._0(main_4__0), ._1(main_4__1), ._2(main_4__2), ._3(main_4__3), ._4(main_4__4), ._5(main_4__5),
    ._6(main_4__6), ._7(main_4__7), ._8(main_4__8), ._9(main_4__9), ._10(main_4__10), .lMan1(main_3_lman1),
    .sMan2_3(main_3_sman2_3), .lMan2(main_3_lman2), .sMan4(main_3_sman4), .lMan3(main_3_lman3),
    .lMan4(main_3_lman4), .sMan5_6(main_3_sman5_6), .lMan5(main_3_lman5), .lMan6(main_3_lman6),
    .sMan7(main_3_sman7), .lMan7(main_3_lman7), .lMan8(main_3_lman8), .sMan8(main_3_sman8),
    .lMan9(main_3_lman9), .sMan9(main_3_sman9), .lMan10(main_3_lman10), .lMan11(main_3_lman11),
    .sMan10(main_3_sman10), .lMan12(main_3_lman12), .sMan11(main_3_sman11));  // open: clock
  Register #(.width(7)) register_2 (.D(main_2__1_char), .en(lchar), .Q(char1), .clk(CLOCK));  // open: clr
  Register #(.width(7)) register_3 (.D(main_2__2_char), .en(lchar), .Q(char2), .clk(CLOCK));  // open: clr
  Register #(.width(7)) register_4 (.D(main_2__3_char), .en(lchar), .Q(char3), .clk(CLOCK));  // open: clr
  Register #(.width(7)) register_5 (.D(main_2__4_char), .en(lchar), .Q(char4), .clk(CLOCK));  // open: clr
  Register #(.width(7)) register_6 (.D(main_2__5_char), .en(lchar), .Q(char5), .clk(CLOCK));  // open: clr
  Register #(.width(7)) register_7 (.D(main_2__6_char), .en(lchar), .Q(char6), .clk(CLOCK));  // open: clr
  Register #(.width(7)) register_8 (.D(main_2__7_char), .en(lchar), .Q(char7), .clk(CLOCK));  // open: clr
  Register #(.width(7)) register_9 (.D(main_2__8_char), .en(lchar), .Q(char8), .clk(CLOCK));  // open: clr
  Counter #(.width(4), .max('hf)) counter_2 (
    .D(false_q), .count(sFalse), .Q(false), .clk(CLOCK));  // open: load, carry, clr
  Counter #(.width(5), .max('h1f)) counter_3 (
    .D(InputWord_q), .count(sconInputWord), .Q(counter_3_q), .clk(CLOCK));  // open: load, carry, clr
  hangmanPrintdataPath_main main_4 (
    .lman1(main_3_lman1), .false(false), .lman2(main_3_lman2), .clock(CLOCK), .sMan2_3(main_3_sman2_3),
    .lman3(main_3_lman3), .sMan4(main_3_sman4), .lman4(main_3_lman4), .sMan5_6(main_3_sman5_6),
    .lman5(main_3_lman5), .lman6(main_3_lman6), .sMan7(main_3_sman7), .lman8(main_3_lman8),
    .lman7(main_3_lman7), .lman9(main_3_lman9), .lman10(main_3_lman10), .sMan8(main_3_sman8),
    .sMan9(main_3_sman9), .sMan10(main_3_sman10), .sMan11(main_3_sman11), .lman11(main_3_lman11),
    .lman12(main_3_lman12), .man1(man1), ._0(main_4__0), .man2(man2), ._1(main_4__1), .man3(man3),
    ._2(main_4__2), .man4(man4), ._3(main_4__3), .man5(man5), ._4(main_4__4), .man6(man6), ._5(main_4__5),
    .man7(man7), ._6(main_4__6), .man8(man8), ._7(main_4__7), .man9(man9), ._8(main_4__8), .man10(man10),
    ._9(main_4__9), .man11(man11), ._10(main_4__10), .man12(man12));
  Counter #(.width(4), .max('hf)) counter_4 (
    .D(scoreUser), .count(sScoreUser), .Q(counter_4_q), .clk(CLOCK));  // open: load, carry, clr
  Comparator #(.width(5)) comparator_1 (.a(counter_3_q), .b(5'b01000), .eq(clockEqu), .lt(clockLess));  // open: gt
  Comparator #(.width(4), .mode("unsigned")) comparator_2 (
    .a(false), .b(4'b1010), .eq(falseEq), .lt(falseLess));  // open: gt
  Counter #(.width(4), .max('hf)) counter_5 (
    .D(controlGame), .count(scontrolGame), .Q(counter_5_q), .clk(CLOCK));  // open: load, carry, clr
  Comparator #(.width(4), .mode("unsigned")) comparator_3 (
    .a(controlGame), .b(size), .eq(controlGAmeEq));  // open: gt, lt
  includeControl_main main_5 (
    .char1(char1), .char2(char2), .char3(char3), .char4(char4), .char5(char5), .char6(char6), .char7(char7),
    .char8(char8), .char(register_10_q), .includeTrue(includeTrue));
  foundedTTYDataPath_main main_6 (
    .char1(char1), .char2(char2), .char3(char3), .char4(char4), .char5(char5), .char6(char6), .char7(char7),
    .char8(char8), .founded(register_10_q), .clock(CLOCK), .char(ttyCharFound));
  WordTTY_main main_7 (
    .char1(char1), .char2(char2), .char3(char3), .char4(char4), .char5(char5), .char6(char6), .char7(char7),
    .char8(char8), .clock(CLOCK), .char(ttyCharword), .reset(resetWordTTY), .print(printWordTTY));
  mainBoard_main main_8 (
    .a(a), .b(b), .c(c), .d(d), .e(e), .f(f), .g(g), .h(h), .i(i), .j(j), .k(k), .l(l), .m(m), .n(n), .o(o),
    .p(p), .q(q), .r(r), .s(s), .t(t), .u(u), .v(v), .w(w), .x(x), .y(y), .z(z), .char(less), .clock(CLOCK));
  Register #(.width(7)) register_10 (.D(less), .en(lcharUser), .Q(register_10_q), .clk(CLOCK));  // open: clr
endmodule
