// Logisim project gameFSM.circ as structural Verilog: 1 circuit, main circuit main
module main (
  input  go,
  input  resetGame,
  input  clockLess,
  input  clockEq,
  input  falseEq,
  input  falseLess,
  input  controlGameEq,
  input  includeTrue,
  input  clock,
  output lScorePc,
  output lScoreUser,
  output lFalse,
  output lControlGAme,
  output llControlInputWord,
  output goInputWord,
  output lChar,
  output lSize,
  output sConInputWord,
  output sControlGame,
  output sFAlse,
  output sScorPC,
  output printWordTTY,
  output resetWordTTY,
  output lCharUser,
  output sScorUser
);

  wire and_1_out, and_2_out, and_3_out, and_4_out, and_5_out, and_6_out, and_7_out, and_8_out, and_9_out,
       and_10_out, and_11_out, and_12_out, and_13_out, and_14_out, and_15_out, and_16_out, and_17_out,
       and_18_out, and_19_out, n1_out, not_1_out, not_2_out, not_3_out, not_4_out, not_5_out, not_6_out,
       not_7_out, not_8_out, not_9_out, not_10_out, not_11_out, not_12_out, not_13_out, not_14_out,
       not_15_out, not_16_out, or_1_out, or_2_out, s1_out, s2_out, xor_1_out, xor_2_out;
  wire [3:0] n0_out, register_1_q;

  not not_1 (not_1_out, go);
  not not_2 (not_2_out, clockLess);
  not not_3 (not_3_out, resetGame);
  not not_4 (not_4_out, falseEq);
  not not_5 (not_5_out, falseLess);
  not not_6 (not_6_out, clockEq);
  not not_7 (not_7_out, controlGameEq);
  not not_8 (not_8_out, includeTrue);
  Register #(.width(4)) register_1 (.D(n0_out), .en(1'b1), .Q(register_1_q), .clk(clock));  // open: clr
  not not_9 (not_9_out, register_1_q[1]);
  not not_10 (not_10_out, register_1_q[2]);
  not not_11 (not_11_out, register_1_q[3]);
  not not_12 (not_12_out, register_1_q[0]);
  xor xor_1 (xor_1_out, falseEq, controlGameEq);
  and and_1 (and_1_out, xor_1_out, not_12_out, not_11_out, register_1_q[2], not_9_out);
  or or_1 (or_1_out, clockLess, clockEq);
  and and_2 (and_2_out, or_1_out, register_1_q[3], not_10_out, not_9_out, register_1_q[0]);
  and and_3 (and_3_out, register_1_q[3], not_10_out, not_9_out, not_12_out);
  and and_4 (and_4_out, not_11_out, register_1_q[2], not_9_out, register_1_q[0]);
  and and_5 (and_5_out, not_11_out, register_1_q[2], register_1_q[1]);
  and and_6 (and_6_out, not_11_out, register_1_q[2], not_9_out, not_12_out, falseLess, not_7_out);
  and and_7 (and_7_out, not_11_out, not_10_out, register_1_q[1], register_1_q[0], clockEq);
  and and_8 (and_8_out, not_11_out, not_10_out, not_9_out, not_12_out, go, not_3_out);
  xor xor_2 (xor_2_out, register_1_q[1], register_1_q[0]);
  and and_9 (and_9_out, xor_2_out, not_11_out, not_10_out);
  and and_10 (and_10_out, not_11_out, not_10_out, register_1_q[1], register_1_q[0], clockLess);
  and and_11 (and_11_out, not_11_out, register_1_q[2], not_9_out, not_12_out, not_5_out, controlGameEq);
  and and_12 (and_12_out, not_11_out, register_1_q[2], not_9_out, register_1_q[0]);
  and and_13 (and_13_out, register_1_q[3], not_10_out, not_9_out, register_1_q[0], clockEq);
  and and_14 (and_14_out, not_11_out, not_10_out, not_9_out, not_12_out, go, resetGame);
  or or_2 (or_2_out, not_12_out, clockLess);
  and and_15 (and_15_out, or_2_out, not_11_out, not_10_out, register_1_q[1]);
  and and_16 (and_16_out, not_11_out, register_1_q[2], not_9_out, not_12_out, not_4_out, controlGameEq);
  and and_17 (and_17_out, not_11_out, register_1_q[2], not_9_out, not_12_out, falseLess, not_7_out);
  and and_18 (and_18_out, not_11_out, register_1_q[2], not_9_out, register_1_q[0], not_8_out);
  or n1 (n1_out, not_12_out, clockLess);
  and and_19 (and_19_out, n1_out, register_1_q[3], not_10_out, not_9_out);
  or n2 (n0_out[2], and_4_out, and_5_out, and_6_out, and_7_out);
  or n3 (n0_out[3], and_1_out, and_2_out, and_3_out);
  or n1_2 (n0_out[1], and_8_out, and_9_out, and_10_out, and_11_out, and_12_out, and_13_out);
  or n0 (n0_out[0], and_14_out, and_15_out, and_16_out, and_17_out, and_18_out, and_19_out);
  not not_13 (not_13_out, register_1_q[0]);
  not not_14 (not_14_out, register_1_q[1]);
  not not_15 (not_15_out, register_1_q[3]);
  not not_16 (not_16_out, register_1_q[2]);
  and s1 (s1_out, not_15_out, not_16_out, not_14_out, register_1_q[0]);
  and s2 (s2_out, not_15_out, not_16_out, register_1_q[1], not_13_out);
  and s3 (goInputWord, not_15_out, not_16_out, register_1_q[1], register_1_q[0]);
  and s5 (lCharUser, not_15_out, register_1_q[2], not_14_out, register_1_q[0]);
  and s6 (sControlGame, not_15_out, register_1_q[2], register_1_q[1], not_13_out);
  and s7 (sFAlse, not_15_out, register_1_q[2], register_1_q[1], register_1_q[0]);
  and s8 (sScorPC, register_1_q[3], not_16_out, not_14_out, not_13_out);
  and s9 (printWordTTY, register_1_q[3], not_16_out, not_14_out, register_1_q[0]);
  and s10 (resetWordTTY, register_1_q[3], not_16_out, register_1_q[1], not_13_out);
  and s11 (sScorUser, register_1_q[3], not_16_out, register_1_q[1], register_1_q[0]);
  or or_3 (lScorePc, s1_out, sScorPC);
  or or_4 (lScoreUser, s1_out, sScorUser);
  or or_5 (lFalse, s2_out, sFAlse);
  or or_6 (lControlGAme, s2_out, sControlGame);
  or or_7 (llControlInputWord, goInputWord, s2_out, sScorPC, printWordTTY);
  or or_8 (sConInputWord, goInputWord, printWordTTY);

  assign lChar = goInputWord;
  assign lSize = goInputWord;
endmodule
