// Logisim project hangmanPrintFSM.circ as structural Verilog: 1 circuit, main circuit main
module main (
  input  _0,
  input  _1,
  input  _2,
  input  _3,
  input  _4,
  input  _5,
  input  _6,
  input  _7,
  input  _8,
  input  _9,
  input  _10,
  input  clock,
  output lMan1,
  output sMan2_3,
  output lMan2,
  output [1:0] sMan4,
  output lMan3,
  output lMan4,
  output [1:0] sMan5_6,
  output lMan5,
  output lMan6,
  output [1:0] sMan7,
  output lMan7,
  output lMan8,
  output [2:0] sMan8,
  output lMan9,
  output [2:0] sMan9,
  output lMan10,
  output lMan11,
  output [1:0] sMan10,
  output lMan12,
  output [1:0] sMan11
);

  wire and_1_out, and_2_out, and_3_out, and_4_out, and_5_out, and_6_out, and_7_out, and_8_out, and_9_out,
       and_10_out, and_11_out, and_12_out, and_13_out, and_14_out, and_15_out, and_16_out, and_17_out,
       and_18_out, and_19_out, and_20_out, and_21_out, and_22_out, not_1_out, not_2_out, not_3_out,
       not_4_out, not_5_out, not_6_out, not_7_out, not_8_out, not_9_out, not_10_out, not_11_out, not_12_out,
       or_1_out, or_2_out, or_3_out, s1_out, s2_out, s3_out, s4_2_out, s4_out, s5_2_out, s5_out, s6_out,
       s7_2_out, s7_out, s8_out, s9_out, s10_out, xor_1_out, xor_2_out, xor_3_out;
  wire [3:0] n0_out, register_1_q;

  Register #(.width(4)) register_1 (.D(n0_out), .en(1'b1), .Q(register_1_q), .clk(clock));  // open: clr
  not not_1 (not_1_out, register_1_q[2]);
  not not_2 (not_2_out, register_1_q[0]);
  not not_3 (not_3_out, register_1_q[1]);
  not not_4 (not_4_out, register_1_q[3]);
  and and_1 (and_1_out, not_4_out, register_1_q[2], register_1_q[1], register_1_q[0]);
  or or_1 (or_1_out, and_1_out, and_2_out);
  and and_2 (and_2_out, register_1_q[3], not_1_out, not_3_out, not_2_out);
  and and_3 (and_3_out, register_1_q[3], not_1_out, not_3_out, _9);
  xor xor_1 (xor_1_out, register_1_q[0], register_1_q[1]);
  and and_4 (and_4_out, register_1_q[3], xor_1_out, not_1_out, _10);
  and and_5 (and_5_out, not_1_out, register_1_q[1], register_1_q[0]);
  or or_2 (or_2_out, and_5_out, and_6_out);
  and and_6 (and_6_out, register_1_q[2], not_3_out, not_2_out);
  and and_7 (and_7_out, not_4_out, register_1_q[2], not_3_out, _5);
  xor xor_2 (xor_2_out, register_1_q[0], register_1_q[1]);
  and and_8 (and_8_out, not_4_out, xor_2_out, register_1_q[2], _6);
  and and_9 (and_9_out, not_4_out, register_1_q[2], register_1_q[1], _7);
  xor xor_3 (xor_3_out, register_1_q[0], register_1_q[1]);
  and and_10 (and_10_out, not_4_out, not_1_out, _2);
  and and_11 (and_11_out, not_4_out, register_1_q[2], _6);
  or or_3 (or_3_out, and_10_out, and_11_out, and_12_out);
  and and_12 (and_12_out, _10, register_1_q[3], not_1_out);
  and and_13 (and_13_out, _3, not_4_out, not_1_out, register_1_q[1]);
  and and_14 (and_14_out, _7, not_4_out, register_1_q[2], register_1_q[1]);
  and and_15 (and_15_out, _1, not_4_out, not_1_out, not_3_out);
  and and_16 (and_16_out, _3, not_4_out, not_1_out, register_1_q[1]);
  and and_17 (and_17_out, _5, not_4_out, register_1_q[2], not_3_out);
  and and_18 (and_18_out, _7, not_4_out, register_1_q[2], register_1_q[1]);
  and and_19 (and_19_out, _9, register_1_q[3], not_1_out, not_3_out);
  and and_20 (and_20_out, or_1_out, _8);
  and and_21 (and_21_out, or_2_out, not_4_out, _4);
  and and_22 (and_22_out, xor_3_out, or_3_out);
  or n3 (n0_out[3], and_20_out, and_3_out, and_4_out);
  or n2 (n0_out[2], and_21_out, and_7_out, and_8_out, and_9_out);
  or n1 (n0_out[1], and_22_out, and_13_out, and_14_out);
  or n0 (n0_out[0], and_15_out, and_16_out, and_17_out, and_18_out, and_19_out);
  not not_5 (not_5_out, register_1_q[3]);
  not not_6 (not_6_out, register_1_q[1]);
  not not_7 (not_7_out, register_1_q[2]);
  not not_8 (not_8_out, register_1_q[0]);
  and s0 (lMan1, not_8_out, not_6_out, not_7_out, not_5_out);
  and s1 (s1_out, register_1_q[0], not_6_out, not_7_out, not_5_out);
  and s2 (s2_out, not_8_out, register_1_q[1], not_7_out, not_5_out);
  and s3 (s3_out, register_1_q[0], register_1_q[1], not_7_out, not_5_out);
  and s4 (s4_out, not_8_out, not_6_out, register_1_q[2], not_5_out);
  and s5 (s5_out, register_1_q[0], not_6_out, register_1_q[2], not_5_out);
  and s6 (s6_out, not_8_out, register_1_q[1], register_1_q[2], not_5_out);
  and s7 (s7_out, register_1_q[0], register_1_q[1], register_1_q[2], not_5_out);
  and s8 (s8_out, not_8_out, not_6_out, not_7_out, register_1_q[3]);
  and s9 (s9_out, register_1_q[0], not_6_out, not_7_out, register_1_q[3]);
  and s10 (s10_out, not_8_out, register_1_q[1], not_7_out, register_1_q[3]);
  or or_4 (lMan2, lMan1, s1_out);
  or or_5 (lMan4, lMan1, s1_out, s2_out);
  or or_6 (lMan5, lMan1, s1_out, s3_out);
  or or_7 (lMan7, lMan1, s3_out, s7_out, s9_out);
  or or_8 (lMan8, lMan7, s5_out);
  or or_9 (lMan9, lMan1, s3_out, s4_out, s5_out, s6_out);
  or or_10 (lMan11, lMan1, s8_out, s10_out);
  or or_11 (lMan10, s5_out, lMan11);
  not not_9 (not_9_out, register_1_q[3]);
  not not_10 (not_10_out, register_1_q[2]);
  not not_11 (not_11_out, register_1_q[1]);
  not not_12 (not_12_out, register_1_q[0]);
  // AND_Gate s0_2 has open pins: in0=not_12_out, in1=not_11_out, in2=not_10_out, in3=not_9_out, out=open
  and s1_2 (sMan2_3, register_1_q[0], not_11_out, not_10_out, not_9_out);
  and s2_2 (sMan4[1], not_12_out, register_1_q[1], not_10_out, not_9_out);
  and s3_2 (sMan5_6[1], register_1_q[0], register_1_q[1], not_10_out, not_9_out);
  and s4_2 (s4_2_out, not_12_out, not_11_out, register_1_q[2], not_9_out);
  and s5_2 (s5_2_out, register_1_q[0], not_11_out, register_1_q[2], not_9_out);
  and s6_2 (sMan9[2], not_12_out, register_1_q[1], register_1_q[2], not_9_out);
  and s7_2 (s7_2_out, register_1_q[0], register_1_q[1], register_1_q[2], not_9_out);
  and s8_2 (sMan11[0], not_12_out, not_11_out, not_10_out, register_1_q[3]);
  and s9_2 (sMan8[2], register_1_q[0], not_11_out, not_10_out, register_1_q[3]);
  and s10_2 (sMan11[1], not_12_out, register_1_q[1], not_10_out, register_1_q[3]);
  or or_12 (sMan8[0], sMan5_6[1], s7_2_out);
  or or_13 (sMan7[0], sMan5_6[1], sMan8[2]);
  or or_14 (sMan7[1], sMan8[2], s7_2_out);
  or or_15 (sMan8[1], s5_2_out, s7_2_out);
  or or_16 (sMan9[0], sMan5_6[1], s5_2_out);
  or or_17 (sMan9[1], s4_2_out, s5_2_out);
  or or_18 (sMan10[0], s5_2_out, sMan11[1]);
  or or_19 (sMan10[1], sMan11[0], sMan11[1]);

  assign lMan3 = lMan2;
  assign lMan6 = lMan5;
  assign lMan12 = lMan1;
  assign sMan4[0] = sMan2_3;
  assign sMan5_6[0] = sMan2_3;

  // Notes on the sheet:
  //   s0
  //   s2
  //   s1
  //   s3
endmodule
