// Logisim project hangmanPrintdataPath.circ as structural Verilog: 1 circuit, main circuit main
module main (
  input  lman1,
  input  [3:0] false,
  input  lman2,
  input  clock,
  input  sMan2_3,
  input  lman3,
  input  [1:0] sMan4,
  input  lman4,
  input  [1:0] sMan5_6,
  input  lman5,
  input  lman6,
  input  [1:0] sMan7,
  input  lman8,
  input  lman7,
  input  lman9,
  input  lman10,
  input  [2:0] sMan8,
  input  [2:0] sMan9,
  input  lman11,
  input  lman12,
  input  [1:0] sMan10,
  input  [1:0] sMan11,
  output [13:0] man1,
  output _0,
  output [13:0] man2,
  output _1,
  output [13:0] man3,
  output _2,
  output [13:0] man4,
  output _3,
  output [13:0] man5,
  output _4,
  output [13:0] man6,
  output _5,
  output [13:0] man7,
  output _6,
  output [13:0] man8,
  output _7,
  output [13:0] man9,
  output _8,
  output [13:0] man10,
  output _9,
  output [13:0] man11,
  output _10,
  output [13:0] man12
);

  wire [13:0] multiplexer_1_out, multiplexer_2_out, multiplexer_3_out, multiplexer_4_out, multiplexer_5_out,
       multiplexer_6_out, multiplexer_7_out, multiplexer_8_out;

  Multiplexer #(.width(14)) multiplexer_1 (
    .in0({14{1'b0}}), .in1(14'h1), .out(multiplexer_1_out), .sel(sMan2_3));  // open: en
  Multiplexer #(.select(2), .width(14)) multiplexer_2 (
    .in0({14{1'b0}}), .in1(14'h1), .in2({14{1'b1}}), .out(multiplexer_2_out), .sel(sMan4));  // open: in3, en
  Multiplexer #(.select(2), .width(14)) multiplexer_3 (
    .in0({14{1'b0}}), .in1(14'h1), .in2(14'h2001), .out(multiplexer_3_out), .sel(sMan5_6));  // open: in3, en
  Multiplexer #(.select(2), .width(14)) multiplexer_4 (
    .in0({14{1'b0}}), .in1(14'h2000), .in2(14'h2040), .in3(14'h2044), .out(multiplexer_4_out), .sel(sMan7));  // open: en
  Multiplexer #(.select(3), .width(14)) multiplexer_5 (
    .in0({14{1'b0}}), .in1(14'h2000), .in2(14'h2e00), .in3(14'h2e80), .in4(14'h2e88),
    .out(multiplexer_5_out), .sel(sMan8));  // open: in5, in6, in7, en
  Multiplexer #(.select(3), .width(14)) multiplexer_6 (
    .in0({14{1'b0}}), .in1(14'h2000), .in2(14'h3000), .in3(14'h3e00), .in4(14'h3ff0),
    .out(multiplexer_6_out), .sel(sMan9));  // open: in5, in6, in7, en
  Multiplexer #(.select(2), .width(14)) multiplexer_7 (
    .in0({14{1'b0}}), .in1(14'he00), .in2(14'he80), .in3(14'he88), .out(multiplexer_7_out), .sel(sMan10));  // open: en
  Multiplexer #(.select(2), .width(14)) multiplexer_8 (
    .in0({14{1'b0}}), .in1(14'h40), .in2(14'h44), .out(multiplexer_8_out), .sel(sMan11));  // open: in3, en
  Register #(.width(14)) u_man1 (.D({14{1'b0}}), .en(lman1), .Q(man1), .clk(clock));  // open: clr
  Register #(.width(14)) u_man2 (.D(multiplexer_1_out), .en(lman2), .Q(man2), .clk(clock));  // open: clr
  Register #(.width(14)) u_man3 (.D(multiplexer_1_out), .en(lman3), .Q(man3), .clk(clock));  // open: clr
  Register #(.width(14)) u_man4 (.D(multiplexer_2_out), .en(lman4), .Q(man4), .clk(clock));  // open: clr
  Register #(.width(14)) u_man5 (.D(multiplexer_3_out), .en(lman5), .Q(man5), .clk(clock));  // open: clr
  Register #(.width(14)) u_man6 (.D(multiplexer_3_out), .en(lman6), .Q(man6), .clk(clock));  // open: clr
  Register #(.width(14)) u_man7 (.D(multiplexer_4_out), .en(lman7), .Q(man7), .clk(clock));  // open: clr
  Register #(.width(14)) u_man8 (.D(multiplexer_5_out), .en(lman8), .Q(man8), .clk(clock));  // open: clr
  Register #(.width(14)) u_man9 (.D(multiplexer_6_out), .en(lman9), .Q(man9), .clk(clock));  // open: clr
  Register #(.width(14)) u_man10 (.D(multiplexer_7_out), .en(lman10), .Q(man10), .clk(clock));  // open: clr
  Register #(.width(14)) u_man11 (.D(multiplexer_8_out), .en(lman11), .Q(man11), .clk(clock));  // open: clr
  Register #(.width(14)) u_man12 (.D({14{1'b0}}), .en(lman12), .Q(man12), .clk(clock));  // open: clr
  Comparator #(.width(4)) comparator_1 (.a(false), .b(4'b0000), .eq(_0));  // open: gt, lt
  Comparator #(.width(4)) comparator_2 (.a(false), .b(4'b0001), .eq(_1));  // open: gt, lt
  Comparator #(.width(4)) comparator_3 (.a(false), .b(4'b0010), .eq(_2));  // open: gt, lt
  Comparator #(.width(4)) comparator_4 (.a(false), .b(4'b0011), .eq(_3));  // open: gt, lt
  Comparator #(.width(4)) comparator_5 (.a(false), .b(4'b0100), .eq(_4));  // open: gt, lt
  Comparator #(.width(4)) comparator_6 (.a(false), .b(4'b0101), .eq(_5));  // open: gt, lt
  Comparator #(.width(4)) comparator_7 (.a(false), .b(4'b0110), .eq(_6));  // open: gt, lt
  Comparator #(.width(4)) comparator_8 (.a(false), .b(4'b0111), .eq(_7));  // open: gt, lt
  Comparator #(.width(4)) comparator_9 (.a(false), .b(4'b1000), .eq(_8));  // open: gt, lt
  Comparator #(.width(4)) comparator_10 (.a(false), .b(4'b1001), .eq(_9));  // open: gt, lt
  Comparator #(.width(4)) comparator_11 (.a(false), .b(4'b1010), .eq(_10));  // open: gt, lt
endmodule
