// Logisim project includeControl.circ as structural Verilog: 1 circuit, main circuit main
module main (
  input  [6:0] char,
  input  [6:0] char1,
  input  [6:0] char2,
  input  [6:0] char3,
  input  [6:0] char4,
  input  [6:0] char5,
  input  [6:0] char6,
  input  [6:0] char7,
  input  [6:0] char8,
  output includeTrue
);

  wire comparator_1_eq, comparator_2_eq, comparator_3_eq, comparator_4_eq, comparator_5_eq, comparator_6_eq,
       comparator_7_eq, comparator_8_eq;

  Comparator #(.width(7), .mode("unsigned")) comparator_1 (.a(char), .b(char1), .eq(comparator_1_eq));  // open: gt, lt
  Comparator #(.width(7), .mode("unsigned")) comparator_2 (.a(char), .b(char2), .eq(comparator_2_eq));  // open: gt, lt
  Comparator #(.width(7), .mode("unsigned")) comparator_3 (.a(char), .b(char3), .eq(comparator_3_eq));  // open: gt, lt
  Comparator #(.width(7), .mode("unsigned")) comparator_4 (.a(char), .b(char4), .eq(comparator_4_eq));  // open: gt, lt
  Comparator #(.width(7), .mode("unsigned")) comparator_5 (.a(char), .b(char5), .eq(comparator_5_eq));  // open: gt, lt
  Comparator #(.width(7), .mode("unsigned")) comparator_6 (.a(char), .b(char6), .eq(comparator_6_eq));  // open: gt, lt
  Comparator #(.width(7), .mode("unsigned")) comparator_7 (.a(char), .b(char7), .eq(comparator_7_eq));  // open: gt, lt
  Comparator #(.width(7), .mode("unsigned")) comparator_8 (.a(char), .b(char8), .eq(comparator_8_eq));  // open: gt, lt
  or or_1 (includeTrue, comparator_1_eq, comparator_2_eq, comparator_3_eq, comparator_4_eq, comparator_5_eq, comparator_6_eq, comparator_7_eq, comparator_8_eq);
endmodule
