// Logisim project inputWordDataPath.circ as structural Verilog: 1 circuit, main circuit main
module main (
  input  l1,
  input  l2,
  input  l3,
  input  [6:0] inputChar,
  input  l4,
  input  l5,
  input  l6,
  input  l7,
  input  l8,
  input  clock,
  output [6:0] _1_char,
  output [6:0] _2_char,
  output [6:0] _3_char,
  output [3:0] size,
  output [6:0] _4_char,
  output [6:0] _5_char,
  output less,
  output [6:0] _6_char,
  output [6:0] _7_char,
  output [6:0] _8_char
);

  wire [6:0] char_q;

  Register #(.width(7)) char (.D(inputChar), .Q(char_q), .clk(clock));  // open: en, clr
  Register #(.width(7)) _1 (.D(char_q), .en(l1), .Q(_1_char), .clk(clock));  // open: clr
  Register #(.width(7)) _2 (.D(char_q), .en(l2), .Q(_2_char), .clk(clock));  // open: clr
  Register #(.width(7)) _3 (.D(char_q), .en(l3), .Q(_3_char), .clk(clock));  // open: clr
  Register #(.width(7)) _4 (.D(char_q), .en(l4), .Q(_4_char), .clk(clock));  // open: clr
  Register #(.width(7)) _5 (.D(char_q), .en(l5), .Q(_5_char), .clk(clock));  // open: clr
  Register #(.width(7)) _6 (.D(char_q), .en(l6), .Q(_6_char), .clk(clock));  // open: clr
  Register #(.width(7)) _7 (.D(char_q), .en(l7), .Q(_7_char), .clk(clock));  // open: clr
  Register #(.width(7)) _8 (.D(char_q), .en(l8), .Q(_8_char), .clk(clock));  // open: clr
  Comparator #(.width(7)) comparator_1 (.a(inputChar), .b({7{1'b0}}), .lt(less));  // open: gt, eq
  Counter #(.width(4), .max('hf)) counter_1 (.count(less), .Q(size), .clk(clock));  // open: load, D, carry, clr
endmodule
