// Logisim project inputWordFSM.circ as structural Verilog: 1 circuit, main circuit main
module main (
  input  goInputWord,
  input  clock,
  output l1,
  output l2,
  output l3,
  output l4,
  output l5,
  output l6,
  output l7,
  output l8
);

  wire and_1_out, and_2_out, and_3_out, and_4_out, and_5_out, and_6_out, and_7_out, and_8_out, not_1_out,
       not_2_out, not_3_out, not_4_out, not_5_out, not_6_out, not_7_out, not_8_out, not_9_out, not_10_out,
       not_11_out, not_12_out, not_13_out;
  wire [3:0] n0_out, register_1_q;

  Register #(.width(4)) register_1 (.D(n0_out), .Q(register_1_q), .clk(clock));  // open: en, clr
  and n3 (n0_out[3], register_1_q[2], register_1_q[1], register_1_q[0]);
  not not_1 (not_1_out, register_1_q[2]);
  not not_2 (not_2_out, register_1_q[1]);
  not not_3 (not_3_out, register_1_q[0]);
  not not_4 (not_4_out, register_1_q[1]);
  not not_5 (not_5_out, register_1_q[0]);
  not not_6 (not_6_out, register_1_q[3]);
  not not_7 (not_7_out, register_1_q[0]);
  not not_8 (not_8_out, register_1_q[0]);
  not not_9 (not_9_out, register_1_q[0]);
  and and_1 (and_1_out, not_1_out, register_1_q[1], register_1_q[0]);
  and and_2 (and_2_out, register_1_q[2], not_2_out);
  and and_3 (and_3_out, register_1_q[2], not_3_out);
  and and_4 (and_4_out, not_4_out, register_1_q[0]);
  and and_5 (and_5_out, register_1_q[1], not_5_out);
  and and_6 (and_6_out, not_6_out, not_7_out, goInputWord);
  and and_7 (and_7_out, register_1_q[1], not_8_out);
  and and_8 (and_8_out, register_1_q[2], not_9_out);
  or n2 (n0_out[2], and_1_out, and_2_out, and_3_out);
  or n1 (n0_out[1], and_4_out, and_5_out);
  or n0 (n0_out[0], and_6_out, and_7_out, and_8_out);
  not not_10 (not_10_out, register_1_q[0]);
  not not_11 (not_11_out, register_1_q[1]);
  not not_12 (not_12_out, register_1_q[3]);
  not not_13 (not_13_out, register_1_q[2]);
  and s1 (l1, not_12_out, not_13_out, not_11_out, register_1_q[0]);
  and s2 (l2, not_12_out, not_13_out, register_1_q[1], not_10_out);
  and s3 (l3, not_12_out, not_13_out, register_1_q[1], register_1_q[0]);
  and s4 (l4, not_12_out, register_1_q[2], not_11_out, not_10_out);
  and s5 (l5, not_12_out, register_1_q[2], not_11_out, register_1_q[0]);
  and s6 (l6, not_12_out, register_1_q[2], register_1_q[1], not_10_out);
  and s7 (l7, not_12_out, register_1_q[2], register_1_q[1], register_1_q[0]);
  and s8 (l8, register_1_q[3], not_13_out, not_11_out, not_10_out);
endmodule
