// Logisim project main.circ as structural Verilog: 1 circuit, main circuit main
module main (
  input  resetGame,
  input  go
);

  wire a_out, b_out, c_out, clock_1_out, d_out, e_out, f_out, g_out, h_out, i_out, j_out, k_out, l_out,
       m_out, main_1_clockequ, main_1_clockless, main_1_controlgameeq, main_1_falseeq, main_1_falseless,
       main_1_includetrue, main_2_goinputword, main_2_lchar, main_2_lcharuser, main_2_lcontrolgame,
       main_2_lfalse, main_2_llcontrolinputword, main_2_lscorepc, main_2_lscoreuser, main_2_lsize,
       main_2_printwordtty, main_2_resetwordtty, main_2_sconinputword, main_2_scontrolgame, main_2_sfalse,
       main_2_sscorpc, main_2_sscoruser, main_3_a_2, main_3_b_2, main_3_c_2, main_3_d_2, main_3_e, main_3_f,
       main_3_g, main_4_a_2, main_4_b_2, main_4_c_2, main_4_d_2, main_4_e, main_4_f, main_4_g, main_5_a_2,
       main_5_b_2, main_5_c_2, main_5_d_2, main_5_e, main_5_f, main_5_g, n_out, o_out, p_out, q_out, r_out,
       s_out, t_out, u_out, v_out, w_out, x_out, y_out, z_out;
  wire [3:0] main_1_scorepc, main_1_scoreuser, main_1_size;
  wire [6:0] keyboard_1_data, main_1_ttycharfound, main_1_ttycharword;
  wire [13:0] main_1_man1, main_1_man2, main_1_man3, main_1_man4, main_1_man5, main_1_man6, main_1_man7,
       main_1_man8, main_1_man9, main_1_man10, main_1_man11, main_1_man12;

  Clock clock_1 (.out(clock_1_out));
  Keyboard keyboard_1 (.clk(clock_1_out), .data(keyboard_1_data));  // open: re, clr, avail
  Button b (.out(b_out));
  Button c (.out(c_out));
  Button a (.out(a_out));
  Button g (.out(g_out));
  Button f (.out(f_out));
  Button d (.out(d_out));
  Button e (.out(e_out));
  Button h (.out(h_out));
  Button j (.out(j_out));
  Button k (.out(k_out));
  Button i (.out(i_out));
  Button m (.out(m_out));
  Button l (.out(l_out));
  Button o (.out(o_out));
  Button n (.out(n_out));
  gameDataPath_main main_1 (
    .CLOCK(clock_1_out), .a(a_out), .lScoreUser(main_2_lscoreuser), .b(b_out), .sScoreUser(main_2_sscoruser),
    .c(c_out), .d(d_out), .lScorePC(main_2_lscorepc), .e(e_out), .sScorePC(main_2_sscorpc), .f(f_out),
    .g(g_out), .lFalse(main_2_lfalse), .h(h_out), .sFalse(main_2_sfalse), .i(i_out), .j(j_out), .k(k_out),
    .lControlGame(main_2_lcontrolgame), .l(l_out), .scontrolGame(main_2_scontrolgame), .m(m_out), .n(n_out),
    .lcontInputWord(main_2_llcontrolinputword), .o(o_out), .sconInputWord(main_2_sconinputword), .p(p_out),
    .q(q_out), .r(r_out), .s(s_out), .char(keyboard_1_data), .t(t_out), .u(u_out), .v(v_out),
    .goInputWord(main_2_goinputword), .w(w_out), .x(x_out), .y(y_out), .z(z_out), .lsize(main_2_lsize),
    .lcharUser(main_2_lcharuser), .scoreUser(main_1_scoreuser), .scorePC(main_1_scorepc),
    .falseEq(main_1_falseeq), .falseLess(main_1_falseless), .controlGAmeEq(main_1_controlgameeq),
    .clockEqu(main_1_clockequ), .clockLess(main_1_clockless), .lchar(main_2_lchar), .size(main_1_size),
    .includeTrue(main_1_includetrue), .ttyCharFound(main_1_ttycharfound), .man1(main_1_man1),
    .ttyCharword(main_1_ttycharword), .man2(main_1_man2), .resetWordTTY(main_2_resetwordtty),
    .printWordTTY(main_2_printwordtty), .man3(main_1_man3), .man9(main_1_man9), .man4(main_1_man4),
    .man10(main_1_man10), .man5(main_1_man5), .man11(main_1_man11), .man6(main_1_man6), .man12(main_1_man12),
    .man7(main_1_man7), .man8(main_1_man8));  // open: false, less, controlGame, char1, char2, char3, char4, char5, char6, char7, char8
  Button r (.out(r_out));
  Button s (.out(s_out));
  Button p (.out(p_out));
  Button q (.out(q_out));
  Button t (.out(t_out));
  Button w (.out(w_out));
  Button v (.out(v_out));
  Button u (.out(u_out));
  gameFSM_main main_2 (
    .go(go), .resetGame(resetGame), .clockLess(main_1_clockless), .clockEq(main_1_clockequ),
    .falseEq(main_1_falseeq), .falseLess(main_1_falseless), .controlGameEq(main_1_controlgameeq),
    .includeTrue(main_1_includetrue), .clock(clock_1_out), .lScorePc(main_2_lscorepc),
    .lScoreUser(main_2_lscoreuser), .lFalse(main_2_lfalse), .lControlGAme(main_2_lcontrolgame),
    .llControlInputWord(main_2_llcontrolinputword), .goInputWord(main_2_goinputword), .lChar(main_2_lchar),
    .lSize(main_2_lsize), .sConInputWord(main_2_sconinputword), .sControlGame(main_2_scontrolgame),
    .sFAlse(main_2_sfalse), .sScorPC(main_2_sscorpc), .printWordTTY(main_2_printwordtty),
    .resetWordTTY(main_2_resetwordtty), .lCharUser(main_2_lcharuser), .sScorUser(main_2_sscoruser));
  Button y (.out(y_out));
  Button x (.out(x_out));
  Button z (.out(z_out));
  TTY #(.rows(5), .cols(20)) tty_1 (.data(main_1_ttycharfound), .clk(clock_1_out));  // open: we, clr
  DotMatrix #(.matrixcols(12), .matrixrows(14)) dotmatrix_1 (
    .col0(main_1_man1), .col1(main_1_man2), .col2(main_1_man3), .col3(main_1_man4), .col4(main_1_man5),
    .col5(main_1_man6), .col6(main_1_man7), .col7(main_1_man8), .col8(main_1_man9), .col9(main_1_man10),
    .col10(main_1_man11), .col11(main_1_man12));
  TTY #(.rows(5), .cols(20)) tty_2 (.data(main_1_ttycharword), .clk(clock_1_out));  // open: we, clr
  _7_segment_main main_3 (
    .D(main_1_size[3]), .C(main_1_size[2]), .B(main_1_size[1]), .A(main_1_size[0]), .a_2(main_3_a_2),
    .b_2(main_3_b_2), .c_2(main_3_c_2), .d_2(main_3_d_2), .e(main_3_e), .f(main_3_f), .g(main_3_g));
  _7_segment_main main_4 (
    .D(main_1_scoreuser[3]), .C(main_1_scoreuser[2]), .B(main_1_scoreuser[1]), .A(main_1_scoreuser[0]),
    .a_2(main_4_a_2), .b_2(main_4_b_2), .c_2(main_4_c_2), .d_2(main_4_d_2), .e(main_4_e), .f(main_4_f),
    .g(main_4_g));
  _7_Segment_Display u_7_segment_display_1 (
    .g(main_4_g), .f(main_4_f), .a(main_4_a_2), .b(main_4_b_2), .e(main_4_e), .d(main_4_d_2), .c(main_4_c_2));  // open: dp
  _7_segment_main main_5 (
    .D(main_1_scorepc[3]), .C(main_1_scorepc[2]), .B(main_1_scorepc[1]), .A(main_1_scorepc[0]),
    .a_2(main_5_a_2), .b_2(main_5_b_2), .c_2(main_5_c_2), .d_2(main_5_d_2), .e(main_5_e), .f(main_5_f),
    .g(main_5_g));
  _7_Segment_Display u_7_segment_display_2 (
    .g(main_3_g), .f(main_3_f), .a(main_3_a_2), .b(main_3_b_2), .e(main_3_e), .d(main_3_d_2), .c(main_3_c_2));  // open: dp
  _7_Segment_Display u_7_segment_display_3 (
    .g(main_5_g), .f(main_5_f), .a(main_5_a_2), .b(main_5_b_2), .e(main_5_e), .d(main_5_d_2), .c(main_5_c_2));  // open: dp

  // Notes on the sheet:
  //   Word
endmodule
