// Logisim project mainBoard.circ as structural Verilog: 1 circuit, main circuit main
module main (
  input  a,
  input  b,
  input  c,
  input  d,
  input  e,
  input  f,
  input  g,
  input  h,
  input  i,
  input  j,
  input  clock,
  input  k,
  input  l,
  input  m,
  input  n,
  input  o,
  input  p,
  input  q,
  input  r,
  input  s,
  input  t,
  input  u,
  input  v,
  input  w,
  input  x,
  input  y,
  input  z,
  output [6:0] char
);

  wire or_1_out, or_2_out, or_3_out, or_4_out;
  wire [1:0] or_6_out;
  wire [6:0] main_1_char, main_2_char, multiplexer_1_out;

  board2_main main_1 (.q(q), .r(r), .s(s), .t(t), .u(u), .v(v), .w(w), .x(x), .y(y), .z(z), .char(main_1_char));
  or or_1 (or_1_out, a, d, b, c, d, f, g, h);
  board_main main_2 (
    .a(a), .b(b), .c(c), .d(d), .e(e), .f(f), .g(g), .h(h), .i(i), .j(j), .k(k), .l(l), .m(m), .n(n), .o(o),
    .p(p), .char(main_2_char));
  or or_2 (or_2_out, q, r, s, t);
  or or_3 (or_3_out, u, v, w, x, y, z);
  or or_4 (or_4_out, i, j, k, l, m, n, o, p);
  or or_5 (or_6_out[1], or_1_out, or_4_out);
  or or_6 (or_6_out[0], or_2_out, or_3_out);
  Multiplexer #(.select(2), .width(7), .enable("false")) multiplexer_1 (
    .in1(main_1_char), .in2(main_2_char), .out(multiplexer_1_out), .sel(or_6_out));  // open: in0, in3
  Register #(.width(7)) register_1 (.D(multiplexer_1_out), .Q(char), .clk(clock));  // open: en, clr
endmodule
