// Logisim project LOGICPROJECT.circ as structural Verilog: 1 circuit, main circuit n3
module n3 (
);

  wire and_1_out, and_2_out, and_3_out, and_5_out, and_6_out, and_7_out, and_9_out, and_10_out, and_11_out,
       and_12_out, and_13_out, and_14_out, and_15_out, and_16_out, and_17_out, and_18_out, and_19_out,
       and_20_out, and_21_out, and_22_out, and_23_out, and_24_out, and_25_out, and_26_out, and_27_out,
       and_28_out, and_29_out, and_30_out, and_31_out, and_32_out, and_33_out, and_34_out, and_35_out,
       and_36_out, and_37_out, and_38_out, and_39_out, and_40_out, and_41_out, and_42_out, and_43_out,
       and_44_out, and_45_out, and_46_out, and_47_out, and_48_out, and_49_out, and_51_out, and_52_out,
       and_53_out, and_55_out, and_56_out, and_57_out, and_58_out, and_59_out, and_60_out, and_61_out,
       and_62_out, and_63_out, and_64_out, and_65_out, and_66_out, and_67_out, and_68_out, button_1_out,
       button_2_out, button_3_out, clock_1_out, clock_2_out, clock_3_out, clock_4_out, clock_5_out,
       clock_6_out, clock_7_out, not_1_out, not_2_out, not_3_out, not_4_out, not_5_out, not_6_out, not_7_out,
       not_8_out, not_9_out, not_10_out, not_11_out, not_12_out, not_13_out, not_14_out, not_15_out,
       not_16_out, not_17_out, not_18_out, not_19_out, not_20_out, not_21_out, not_22_out, not_23_out,
       not_24_out, not_25_out, not_26_out, not_27_out, not_28_out, not_29_out, not_30_out, not_31_out,
       not_32_out, not_33_out, not_34_out, not_35_out, not_36_out, not_37_out, not_38_out, not_39_out,
       not_40_out, not_41_out, not_42_out, not_43_out, not_44_out, not_45_out, not_46_out, not_47_out,
       not_48_out, not_49_out, not_50_out, not_51_out, not_52_out, not_53_out, not_54_out, not_55_out,
       not_56_out, not_57_out, not_58_out, not_59_out, not_60_out, not_61_out, not_62_out, not_63_out,
       not_64_out, not_65_out, not_66_out, not_67_out, not_68_out, not_69_out, not_70_out, not_71_out,
       not_72_out, not_73_out, not_74_out, not_75_out, not_76_out, not_77_out, not_78_out, not_79_out,
       not_80_out, not_81_out, not_82_out, not_83_out, not_84_out, not_85_out, not_86_out, not_87_out,
       not_88_out, not_89_out, not_90_out, not_91_out, not_92_out, not_93_out, not_94_out, not_95_out;
  wire [1:0] and_4_out, and_8_out, and_50_out, and_54_out, STATE_2_q, STATE_4_q, STATE_5_q, STATE_q;
  wire [2:0] or_5_out, STATE_3_q;
  wire [3:0] or_9_out, or_13_out, register_1_q, register_2_q;

  Button button_1 (.out(button_1_out));
  Button button_2 (.out(button_2_out));
  Clock clock_1 (.out(clock_1_out));
  Clock clock_2 (.out(clock_2_out));
  Register #(.width(2)) STATE (.D(and_4_out), .en(1'b1), .Q(STATE_q), .clk(clock_1_out));  // open: clr
  Register #(.width(2)) STATE_2 (.D(and_8_out), .en(1'b1), .Q(STATE_2_q), .clk(clock_2_out));  // open: clr
  not not_1 (not_1_out, STATE_q[1]);
  not not_2 (not_2_out, STATE_q[1]);
  not not_3 (not_3_out, STATE_q[0]);
  not not_4 (not_4_out, STATE_q[1]);
  not not_5 (not_5_out, STATE_q[0]);
  not not_6 (not_6_out, STATE_2_q[1]);
  not not_7 (not_7_out, STATE_2_q[1]);
  not not_8 (not_8_out, STATE_2_q[0]);
  not not_9 (not_9_out, STATE_2_q[1]);
  not not_10 (not_10_out, STATE_2_q[0]);
  Clock clock_3 (.out(clock_3_out));
  and and_1 (and_1_out, not_1_out, STATE_q[0]);
  and and_2 (and_2_out, button_1_out, not_2_out, STATE_q[0]);
  and and_3 (and_3_out, button_1_out, not_3_out, STATE_q[1]);
  and and_4 (and_4_out[0], button_1_out, not_4_out, not_5_out);
  and and_5 (and_5_out, not_6_out, STATE_2_q[0]);
  and and_6 (and_6_out, button_2_out, not_7_out, STATE_2_q[0]);
  and and_7 (and_7_out, button_2_out, not_8_out, STATE_2_q[1]);
  and and_8 (and_8_out[0], button_2_out, not_9_out, not_10_out);
  Register #(.width(3)) STATE_3 (.D(or_5_out), .en(1'b1), .Q(STATE_3_q), .clk(clock_3_out));  // open: clr
  or or_1 (and_4_out[1], and_2_out, and_3_out);
  or or_2 (and_8_out[1], and_6_out, and_7_out);
  Button button_3 (.out(button_3_out));
  not not_11 (not_11_out, STATE_3_q[1]);
  not not_12 (not_12_out, STATE_3_q[0]);
  not not_13 (not_13_out, and_5_out);
  not not_14 (not_14_out, button_3_out);
  not not_15 (not_15_out, and_5_out);
  not not_16 (not_16_out, button_3_out);
  not not_17 (not_17_out, button_3_out);
  not not_18 (not_18_out, button_3_out);
  not not_19 (not_19_out, button_3_out);
  not not_20 (not_20_out, STATE_3_q[2]);
  not not_21 (not_21_out, and_1_out);
  not not_22 (not_22_out, button_3_out);
  not not_23 (not_23_out, and_1_out);
  not not_24 (not_24_out, button_3_out);
  not not_25 (not_25_out, button_3_out);
  not not_26 (not_26_out, button_3_out);
  not not_27 (not_27_out, and_5_out);
  not not_28 (not_28_out, button_3_out);
  not not_29 (not_29_out, button_3_out);
  not not_30 (not_30_out, STATE_3_q[2]);
  not not_31 (not_31_out, STATE_3_q[0]);
  not not_32 (not_32_out, and_1_out);
  not not_33 (not_33_out, button_3_out);
  not not_34 (not_34_out, and_5_out);
  not not_35 (not_35_out, and_1_out);
  not not_36 (not_36_out, button_3_out);
  not not_37 (not_37_out, button_3_out);
  not not_38 (not_38_out, STATE_3_q[2]);
  not not_39 (not_39_out, and_5_out);
  not not_40 (not_40_out, button_3_out);
  not not_41 (not_41_out, button_3_out);
  not not_42 (not_42_out, STATE_3_q[1]);
  not not_43 (not_43_out, STATE_3_q[0]);
  not not_44 (not_44_out, and_5_out);
  not not_45 (not_45_out, button_3_out);
  and and_9 (and_9_out, not_11_out, not_12_out, not_13_out, and_1_out, not_14_out);
  and and_10 (and_10_out, STATE_3_q[2], not_15_out, not_16_out);
  and and_11 (and_11_out, STATE_3_q[2], and_1_out, not_17_out);
  and and_12 (and_12_out, STATE_3_q[2], STATE_3_q[0], not_18_out);
  and and_13 (and_13_out, STATE_3_q[2], STATE_3_q[1], not_19_out);
  and and_14 (and_14_out, not_20_out, STATE_3_q[0], and_5_out, not_21_out, not_22_out);
  and and_15 (and_15_out, STATE_3_q[1], not_23_out, not_24_out);
  and and_16 (and_16_out, STATE_3_q[1], and_5_out, not_25_out);
  and and_17 (and_17_out, STATE_3_q[1], STATE_3_q[0], not_26_out);
  and and_18 (and_18_out, STATE_3_q[2], STATE_3_q[0], not_27_out, and_1_out, not_28_out);
  and and_19 (and_19_out, STATE_3_q[2], STATE_3_q[1], not_29_out);
  and and_20 (and_20_out, not_30_out, not_31_out, and_5_out, not_32_out, not_33_out);
  and and_21 (and_21_out, STATE_3_q[0], not_34_out, not_35_out, not_36_out);
  and and_22 (and_22_out, STATE_3_q[0], and_5_out, and_1_out, not_37_out);
  and and_23 (and_23_out, not_38_out, STATE_3_q[1], not_39_out, and_1_out, not_40_out);
  and and_24 (and_24_out, STATE_3_q[1], STATE_3_q[0], not_41_out);
  and and_25 (and_25_out, STATE_3_q[2], not_42_out, not_43_out, not_44_out, and_1_out, not_45_out);
  or or_3 (or_5_out[2], and_9_out, and_10_out, and_11_out, and_12_out, and_13_out);
  or or_4 (or_5_out[1], and_14_out, and_15_out, and_16_out, and_17_out, and_18_out, and_19_out);
  or or_5 (or_5_out[0], and_20_out, and_21_out, and_22_out, and_23_out, and_24_out, and_25_out);
  Clock clock_4 (.out(clock_4_out));
  not not_46 (not_46_out, STATE_3_q[1]);
  not not_47 (not_47_out, STATE_3_q[0]);
  not not_48 (not_48_out, STATE_3_q[2]);
  not not_49 (not_49_out, STATE_3_q[1]);
  not not_50 (not_50_out, STATE_3_q[0]);
  not not_51 (not_51_out, STATE_3_q[2]);
  not not_52 (not_52_out, STATE_3_q[0]);
  not not_53 (not_53_out, STATE_3_q[2]);
  Register #(.width(4)) register_1 (.D(or_9_out), .en(1'b1), .Q(register_1_q), .clk(clock_4_out));  // open: clr
  Hex_Digit_Display hex_digit_display_1 (.value(register_1_q));  // open: dp
  and and_26 (and_26_out, STATE_3_q[2], STATE_3_q[1], not_54_out);
  not not_54 (not_54_out, STATE_3_q[0]);
  not not_55 (not_55_out, STATE_3_q[1]);
  and and_27 (and_27_out, STATE_3_q[2], not_55_out, STATE_3_q[0]);
  and and_28 (and_28_out, STATE_3_q[2], not_46_out, not_47_out);
  and and_29 (and_29_out, not_48_out, not_49_out, not_50_out);
  not not_56 (not_56_out, STATE_3_q[2]);
  not not_57 (not_57_out, STATE_3_q[1]);
  and and_30 (and_30_out, not_56_out, not_57_out, STATE_3_q[0]);
  and and_31 (and_31_out, not_51_out, STATE_3_q[1], not_52_out);
  and and_32 (and_32_out, not_53_out, STATE_3_q[1], STATE_3_q[0]);
  Hex_Digit_Display hex_digit_display_2 (.value(register_2_q));  // open: dp
  LED led_1 (.in(and_26_out));
  LED led_2 (.in(and_27_out));
  LED led_3 (.in(and_28_out));
  LED led_4 (.in(and_29_out));
  LED led_5 (.in(and_30_out));
  LED led_6 (.in(and_31_out));
  LED led_7 (.in(and_32_out));
  not not_58 (not_58_out, register_1_q[3]);
  not not_59 (not_59_out, register_1_q[2]);
  not not_60 (not_60_out, register_1_q[1]);
  not not_61 (not_61_out, register_1_q[0]);
  not not_62 (not_62_out, and_47_out);
  not not_63 (not_63_out, register_1_q[2]);
  not not_64 (not_64_out, register_1_q[1]);
  not not_65 (not_65_out, register_1_q[0]);
  not not_66 (not_66_out, and_47_out);
  not not_67 (not_67_out, register_1_q[1]);
  not not_68 (not_68_out, register_1_q[0]);
  not not_69 (not_69_out, and_47_out);
  not not_70 (not_70_out, register_1_q[0]);
  not not_71 (not_71_out, and_47_out);
  and and_33 (and_33_out, not_58_out, register_1_q[2], register_1_q[1], register_1_q[0], and_47_out);
  and and_34 (and_34_out, register_1_q[3], not_59_out);
  and and_35 (and_35_out, register_1_q[3], not_60_out);
  and and_36 (and_36_out, register_1_q[3], not_61_out);
  and and_37 (and_37_out, register_1_q[3], not_62_out);
  and and_38 (and_38_out, not_63_out, register_1_q[1], register_1_q[0], and_47_out);
  and and_39 (and_39_out, register_1_q[2], not_64_out);
  and and_40 (and_40_out, register_1_q[2], not_65_out);
  and and_41 (and_41_out, register_1_q[2], not_66_out);
  and and_42 (and_42_out, not_67_out, register_1_q[0], and_47_out);
  and and_43 (and_43_out, register_1_q[1], not_68_out);
  and and_44 (and_44_out, register_1_q[1], not_69_out);
  and and_45 (and_45_out, not_70_out, and_47_out);
  and and_46 (and_46_out, register_1_q[0], not_71_out);
  or or_6 (or_9_out[3], and_33_out, and_34_out, and_35_out, and_36_out, and_37_out);
  or or_7 (or_9_out[2], and_38_out, and_39_out, and_40_out, and_41_out);
  or or_8 (or_9_out[1], and_42_out, and_43_out, and_44_out);
  or or_9 (or_9_out[0], and_45_out, and_46_out);
  Clock clock_5 (.out(clock_5_out));
  Clock clock_6 (.out(clock_6_out));
  Register #(.width(2)) STATE_4 (.D(and_54_out), .en(1'b1), .Q(STATE_4_q), .clk(clock_5_out));  // open: clr
  Clock clock_7 (.out(clock_7_out));
  Register #(.width(2)) STATE_5 (.D(and_50_out), .en(1'b1), .Q(STATE_5_q), .clk(clock_6_out));  // open: clr
  not not_72 (not_72_out, STATE_4_q[1]);
  not not_73 (not_73_out, STATE_4_q[1]);
  not not_74 (not_74_out, STATE_4_q[0]);
  not not_75 (not_75_out, STATE_4_q[1]);
  not not_76 (not_76_out, STATE_4_q[0]);
  Register #(.width(4)) register_2 (.D(or_13_out), .en(1'b1), .Q(register_2_q), .clk(clock_7_out));  // open: clr
  not not_77 (not_77_out, STATE_5_q[1]);
  and and_47 (and_47_out, not_77_out, STATE_5_q[0]);
  and and_48 (and_48_out, and_26_out, not_78_out, STATE_5_q[0]);
  not not_78 (not_78_out, STATE_5_q[1]);
  not not_79 (not_79_out, STATE_5_q[0]);
  and and_49 (and_49_out, and_26_out, not_79_out, STATE_5_q[1]);
  not not_80 (not_80_out, STATE_5_q[1]);
  and and_50 (and_50_out[0], and_26_out, not_80_out, not_81_out);
  not not_81 (not_81_out, STATE_5_q[0]);
  and and_51 (and_51_out, not_72_out, STATE_4_q[0]);
  and and_52 (and_52_out, and_32_out, not_73_out, STATE_4_q[0]);
  and and_53 (and_53_out, and_32_out, not_74_out, STATE_4_q[1]);
  and and_54 (and_54_out[0], and_32_out, not_75_out, not_76_out);
  or or_10 (and_50_out[1], and_48_out, and_49_out);
  or or_11 (and_54_out[1], and_52_out, and_53_out);
  not not_82 (not_82_out, register_2_q[3]);
  not not_83 (not_83_out, register_2_q[2]);
  not not_84 (not_84_out, register_2_q[1]);
  not not_85 (not_85_out, register_2_q[0]);
  not not_86 (not_86_out, and_51_out);
  not not_87 (not_87_out, register_2_q[2]);
  not not_88 (not_88_out, register_2_q[1]);
  not not_89 (not_89_out, register_2_q[0]);
  not not_90 (not_90_out, and_51_out);
  not not_91 (not_91_out, register_2_q[1]);
  and and_55 (and_55_out, not_91_out, register_2_q[0], and_51_out);
  and and_56 (and_56_out, register_2_q[1], not_92_out);
  not not_92 (not_92_out, register_2_q[0]);
  and and_57 (and_57_out, register_2_q[1], not_93_out);
  not not_93 (not_93_out, and_51_out);
  not not_94 (not_94_out, register_2_q[0]);
  and and_58 (and_58_out, not_94_out, and_51_out);
  and and_59 (and_59_out, register_2_q[0], not_95_out);
  not not_95 (not_95_out, and_51_out);
  and and_60 (and_60_out, not_82_out, register_2_q[2], register_2_q[1], register_2_q[0], and_51_out);
  and and_61 (and_61_out, register_2_q[3], not_83_out);
  and and_62 (and_62_out, register_2_q[3], not_84_out);
  and and_63 (and_63_out, register_2_q[3], not_85_out);
  and and_64 (and_64_out, register_2_q[3], not_86_out);
  and and_65 (and_65_out, not_87_out, register_2_q[1], register_2_q[0], and_51_out);
  and and_66 (and_66_out, register_2_q[2], not_88_out);
  and and_67 (and_67_out, register_2_q[2], not_89_out);
  and and_68 (and_68_out, register_2_q[2], not_90_out);
  or or_12 (or_13_out[1], and_55_out, and_56_out, and_57_out);
  or or_13 (or_13_out[0], and_58_out, and_59_out);
  or or_14 (or_13_out[3], and_60_out, and_61_out, and_62_out, and_63_out, and_64_out);
  or or_15 (or_13_out[2], and_65_out, and_66_out, and_67_out, and_68_out);

  // Notes on the sheet:
  //   BUTTON0
  //   BUTTON1
  //   N0
  //   N0
  //   N1
  //   N1
  //   B0
  //   B1
  //   RESET
  //   N2
  //   N1
  //   N0
  //   S1
  //   S0
  //   INPUT1
  //   S2
  //   BUTTON 0
  //   LAMP2
  //   BUTTON 1
  //   LAMP1
  //   LAMP3
  //   LAMP4
  //   LAMP5
  //   LAM6
  //   LAMP7
  //   n3
  //   n2
  //   n1
  //   n0
  //   N0
  //   N0
  //   N1
  //   N1
  //   INPUT7
endmodule
