// Logisim project Main.circ as structural Verilog: 1 circuit, main circuit main
module main (
  input  [15:0] MULT,
  input  [15:0] _0_Constant,
  input  [15:0] A,
  input  GO,
  input  [15:0] B,
  input  [15:0] minus_1_Constant,
  output [15:0] RESULT,
  output [2:0] STATE
);

  wire clock_1_out, Control_Unit_la, Control_Unit_lb, Control_Unit_lm, Control_Unit_lr, Control_Unit_sa0,
       Control_Unit_sa1, Control_Unit_sb, Control_Unit_sb_1, Control_Unit_sm, Control_Unit_sma, Data_Path_eq,
       Data_Path_gt, Data_Path_lt;

  Clock clock_1 (.out(clock_1_out));
  controlUnit_main Control_Unit (
    .go(GO), .Lt(Data_Path_lt), .Eq(Data_Path_eq), .Gt(Data_Path_gt), .CLK(clock_1_out),
    .Sm(Control_Unit_sm), .Sa1(Control_Unit_sa1), .Sa0(Control_Unit_sa0), .Sb(Control_Unit_sb),
    .Sma(Control_Unit_sma), .Sb_1(Control_Unit_sb_1), .Lm(Control_Unit_lm), .La(Control_Unit_la),
    .Lb(Control_Unit_lb), .Lr(Control_Unit_lr), .STATE(STATE));
  datapath_main Data_Path (
    ._0__Constant(_0_Constant), .a_i(A), .Sa0(Control_Unit_sa0), .Sa1(Control_Unit_sa1),
    .La(Control_Unit_la), .Mult(MULT), .Sm(Control_Unit_sm), .Sma(Control_Unit_sma), .Lm(Control_Unit_lm),
    .b_i(B), .Sb(Control_Unit_sb), .Lr(Control_Unit_lr), .Lb(Control_Unit_lb), .Sb_1(Control_Unit_sb_1),
    .minus_1_Constant(minus_1_Constant), .CLK(clock_1_out), .Gt(Data_Path_gt), .Eq(Data_Path_eq),
    .Lt(Data_Path_lt), .Result(RESULT));

  // Notes on the sheet:
  //   Mult and 0 (constant) must be loaded 0, -1 (constant) must be loaded before starting the program.
endmodule
