// Logisim project controlUnit.circ as structural Verilog: 1 circuit, main circuit main
module main (
  input  go,
  input  Lt,
  input  Eq,
  input  Gt,
  input  CLK,
  output Sm,
  output Sa1,
  output Sa0,
  output Sb,
  output Sma,
  output Sb_1,
  output Lm,
  output La,
  output Lb,
  output Lr,
  output [2:0] STATE
);

  wire and_1_out, and_2_out, and_3_out, and_4_out, and_5_out, and_6_out, and_7_out, and_8_out, not_1_out,
       not_2_out, not_3_out, not_4_out, not_5_out, not_6_out, or_1_out, or_2_out, S3_out;
  wire [2:0] N0_out;

  Register #(.width(3)) u_STATE (.D(N0_out), .en(1'b1), .Q(STATE), .clk(CLK));  // open: clr
  not not_1 (not_1_out, STATE[1]);
  not not_2 (not_2_out, STATE[2]);
  not not_3 (not_3_out, STATE[0]);
  and and_1 (and_1_out, STATE[1], not_2_out, not_3_out, Lt);
  and and_2 (and_2_out, not_2_out, STATE[1], not_3_out, Eq);
  and and_3 (and_3_out, not_2_out, STATE[1], STATE[0]);
  or or_1 (or_1_out, Gt, Eq);
  or or_2 (or_2_out, Gt, Lt);
  and and_4 (and_4_out, or_1_out, not_3_out, STATE[1], not_2_out);
  and and_5 (and_5_out, STATE[2], not_1_out);
  and and_6 (and_6_out, not_2_out, not_1_out, STATE[0]);
  and and_7 (and_7_out, or_2_out, not_3_out, not_2_out, STATE[1]);
  and and_8 (and_8_out, not_2_out, not_1_out, not_3_out, go);
  or N2 (N0_out[2], and_1_out, and_2_out, and_3_out);
  or N1 (N0_out[1], and_4_out, and_5_out, and_6_out);
  or N0 (N0_out[0], and_7_out, and_8_out);
  not not_4 (not_4_out, STATE[0]);
  not not_5 (not_5_out, STATE[2]);
  not not_6 (not_6_out, STATE[1]);
  and S1 (Sa0, not_5_out, not_6_out, STATE[0]);
  and S3 (S3_out, not_5_out, STATE[1], STATE[0]);
  and S4 (Sb_1, STATE[2], not_6_out, not_4_out);
  and S5 (Sa1, STATE[2], not_6_out, STATE[0]);
  and S6 (Lr, STATE[2], STATE[1], not_4_out);
  or or_3 (Lm, Sb_1, Sa0);
  or or_4 (La, Sa0, S3_out, Sa1);
  or or_5 (Lb, Sa0, Sa1);

  assign Sb = Sa0;
  assign Sm = Sa0;
  assign Sma = Sb_1;

  // Notes on the sheet:
  //   go
  //   Lt
  //   Gt
  //   Eq
  //   P2
  //   P1
  //   P0
  //   P1'
  //   P2'
  //   P0'
  //   P1
  //   P2
  //   P0
  //   P2'
  //   P1'
  //   P0'
  //   S1+S4
  //   S1+S3+S5
  //   S1+S5
endmodule
