// Logisim project datapath.circ as structural Verilog: 1 circuit, main circuit main
module main (
  input  [15:0] _0__Constant,
  input  [15:0] a_i,
  input  Sa0,
  input  Sa1,
  input  La,
  input  [15:0] Mult,
  input  Sm,
  input  Sma,
  input  Lm,
  input  [15:0] b_i,
  input  Sb,
  input  Lr,
  input  Lb,
  input  Sb_1,
  input  [15:0] minus_1_Constant,
  input  CLK,
  output Gt,
  output Eq,
  output Lt,
  output [15:0] Result
);

  wire [15:0] A_q, adder_1_out, B_q, Mult_q, multiplexer_1_out, multiplexer_2_out, multiplexer_3_out,
       multiplexer_4_out, multiplexer_5_out, negator_1_out, negator_2_out;

  Negator #(.width(16)) negator_1 (.in(a_i), .out(negator_1_out));
  Negator #(.width(16)) negator_2 (.in(b_i), .out(negator_2_out));
  Multiplexer #(.select(2), .width(16), .enable("false")) multiplexer_1 (
    .in0(adder_1_out), .in1(a_i), .in2(negator_1_out), .out(multiplexer_1_out), .sel({Sa1, Sa0}));  // open: in3
  Multiplexer #(.width(16), .enable("false")) multiplexer_2 (
    .in0(adder_1_out), .in1(Mult), .out(multiplexer_2_out), .sel(Sm));
  Multiplexer #(.width(16), .enable("false")) multiplexer_3 (
    .in0(negator_2_out), .in1(b_i), .out(multiplexer_3_out), .sel(Sb));
  Register #(.width(16)) A (.D(multiplexer_1_out), .en(La), .Q(A_q), .clk(CLK));  // open: clr
  Register #(.width(16)) u_Mult (.D(multiplexer_2_out), .en(Lm), .Q(Mult_q), .clk(CLK));  // open: clr
  Register #(.width(16)) B (.D(multiplexer_3_out), .en(Lb), .Q(B_q), .clk(CLK));  // open: clr
  Comparator #(.width(16)) comparator_1 (.a(A_q), .b(_0__Constant), .gt(Gt), .eq(Eq), .lt(Lt));
  Multiplexer #(.width(16), .enable("false")) multiplexer_4 (
    .in0(A_q), .in1(Mult_q), .out(multiplexer_4_out), .sel(Sma));
  Multiplexer #(.width(16), .enable("false")) multiplexer_5 (
    .in0(minus_1_Constant), .in1(B_q), .out(multiplexer_5_out), .sel(Sb_1));
  Adder #(.width(16)) adder_1 (
    .a(multiplexer_4_out), .b(multiplexer_5_out), .out(adder_1_out), .cin(1'b0));  // open: cout
  Register #(.width(16)) u_Result (.D(Mult_q), .en(Lr), .Q(Result), .clk(CLK));  // open: clr

  // Notes on the sheet:
  //   B
  //   A
  //   Mult
  //   mult+b || a -1
  //   mult + b
  //   a - 1
endmodule
