// Logisim project lab3.circ as structural Verilog: 1 circuit, main circuit main
module main (
  input  A,
  input  B
);

  wire and_1_out, and_2_out, and_3_out, and_4_out, and_5_out, and_6_out, and_7_out, clock_1_out, not_1_out,
       not_2_out, not_3_out, not_4_out, not_5_out, or_1_out, s2_out, s3_out, xnor_1_out;
  wire [1:0] n0_out, register_1_q;

  not not_1 (not_1_out, B);
  not not_2 (not_2_out, A);
  Register #(.width(2)) register_1 (.D(n0_out), .Q(register_1_q), .clk(clock_1_out));  // open: en, clr
  Clock clock_1 (.out(clock_1_out));
  not not_3 (not_3_out, register_1_q[0]);
  not not_4 (not_4_out, register_1_q[1]);
  and and_1 (and_1_out, register_1_q[0], register_1_q[1], B);
  and and_2 (and_2_out, not_4_out, A, not_1_out);
  and and_3 (and_3_out, register_1_q[1], not_3_out, not_2_out, B);
  and and_4 (and_4_out, not_4_out, register_1_q[0], A);
  and and_5 (and_5_out, register_1_q[1], not_3_out, not_2_out, B);
  and and_6 (and_6_out, register_1_q[0], register_1_q[1], B);
  xnor xnor_1 (xnor_1_out, B, A);
  or n0 (n0_out[0], and_2_out, and_1_out, and_3_out);
  and and_7 (and_7_out, register_1_q[1], xnor_1_out, not_3_out);
  or N1 (n0_out[1], and_4_out, and_6_out, and_7_out, and_5_out);
  not not_5 (not_5_out, register_1_q[0]);
  and s2 (s2_out, register_1_q[1], not_5_out);
  or or_1 (or_1_out, s2_out, s3_out);
  and s3 (s3_out, register_1_q[0], register_1_q[1]);
  LED led_1 (.in(or_1_out));
endmodule
