// Logisim project lab4.circ as structural Verilog: 1 circuit, main circuit main
module main (
  input  p3s,
  input  p7s,
  input  p37s,
  input  req
);

  wire and_1_out, and_2_out, and_3_out, and_4_out, and_5_out, and_6_out, and_7_out, and_8_out, and_9_out,
       and_10_out, and_11_out, and_12_out, and_13_out, clock_1_out, not_1_out, not_2_out, not_3_out,
       not_4_out, not_5_out, not_6_out, not_7_out, not_8_out, not_9_out, or_1_out, or_2_out;
  wire [2:0] n0_out, register_1_q;

  Register #(.width(3)) register_1 (.D(n0_out), .Q(register_1_q), .clk(clock_1_out));  // open: en, clr
  Clock clock_1 (.out(clock_1_out));
  not not_1 (not_1_out, register_1_q[0]);
  not not_2 (not_2_out, register_1_q[1]);
  not not_3 (not_3_out, register_1_q[2]);
  and n2 (n0_out[2], not_3_out, register_1_q[1], register_1_q[0], p37s);
  and and_1 (and_1_out, not_3_out, register_1_q[1], not_1_out);
  and and_2 (and_2_out, not_3_out, not_2_out, register_1_q[0], p3s);
  and and_3 (and_3_out, not_3_out, register_1_q[1], register_1_q[0], not_4_out);
  not not_4 (not_4_out, p37s);
  and and_4 (and_4_out, register_1_q[0], not_5_out);
  not not_5 (not_5_out, p37s);
  and and_5 (and_5_out, not_1_out, p7s);
  not not_6 (not_6_out, p3s);
  and and_6 (and_6_out, not_6_out, register_1_q[0]);
  and and_7 (and_7_out, not_1_out, req);
  or or_1 (or_1_out, and_4_out, and_5_out);
  or or_2 (or_2_out, and_6_out, and_7_out);
  or n1 (n0_out[1], and_1_out, and_2_out, and_3_out);
  and and_8 (and_8_out, or_1_out, not_3_out, register_1_q[1]);
  and and_9 (and_9_out, or_2_out, not_3_out, not_2_out);
  or n0 (n0_out[0], and_8_out, and_9_out);
  not not_7 (not_7_out, register_1_q[2]);
  not not_8 (not_8_out, register_1_q[1]);
  not not_9 (not_9_out, register_1_q[0]);
  and and_10 (and_10_out, not_7_out, not_8_out);
  and and_11 (and_11_out, not_7_out, register_1_q[1], not_9_out);
  and and_12 (and_12_out, not_7_out, register_1_q[1], register_1_q[0]);
  and and_13 (and_13_out, register_1_q[2], not_8_out, not_9_out);
  LED led_1 (.in(and_10_out));
  LED led_2 (.in(and_11_out));
  LED led_3 (.in(and_12_out));
  LED led_4 (.in(and_13_out));

  // Notes on the sheet:
  //   red
  //   orange
  //   green
  //   resetT
endmodule
