// Logisim project lab5_datapath.circ as structural Verilog: 1 circuit, main circuit main
module main (
  input  resetT,
  input  clock,
  input  [6:0] _3,
  input  [6:0] _7,
  input  [6:0] _37,
  output p3s,
  output p7s,
  output p37s
);

  wire comparator_1_eq, comparator_1_gt, comparator_2_eq, comparator_2_gt;
  wire [6:0] counter_1_q;

  Counter #(.width(7), .max('h7f)) counter_1 (
    .count(clock), .Q(counter_1_q), .clk(clock), .clr(resetT));  // open: load, D, carry
  Comparator #(.width(7), .mode("unsigned")) comparator_1 (
    .a(counter_1_q), .b(_3), .gt(comparator_1_gt), .eq(comparator_1_eq));  // open: lt
  or or_1 (p3s, comparator_1_gt, comparator_1_eq);
  Comparator #(.width(7), .mode("unsigned")) comparator_2 (
    .a(counter_1_q), .b(_7), .gt(comparator_2_gt), .eq(comparator_2_eq));  // open: lt
  or or_2 (p7s, comparator_2_gt, comparator_2_eq);
  Comparator #(.width(7), .mode("unsigned")) comparator_3 (.a(counter_1_q), .b(_37), .eq(p37s));  // open: gt, lt
endmodule
