// Logisim project lab5_fsm.circ as structural Verilog: 1 circuit, main circuit main
module main (
  input  p3s,
  input  p7s,
  input  p37s,
  input  req,
  input  clock,
  output red,
  output orange,
  output green,
  output resetT
);

  wire and_1_out, and_2_out, and_3_out, and_4_out, and_5_out, and_6_out, and_7_out, and_8_out, and_9_out,
       not_1_out, not_2_out, not_3_out, not_4_out, not_5_out, not_6_out, not_7_out;
  wire [1:0] N0_out, register_1_q;

  not not_1 (not_1_out, p37s);
  not not_2 (not_2_out, p3s);
  not not_3 (not_3_out, p7s);
  not not_4 (not_4_out, register_1_q[1]);
  not not_5 (not_5_out, register_1_q[0]);
  Register #(.width(2)) register_1 (.D(N0_out), .Q(register_1_q), .clk(clock));  // open: en, clr
  and and_1 (and_1_out, register_1_q[1], not_5_out);
  and and_2 (and_2_out, not_4_out, register_1_q[0], p3s);
  and and_3 (and_3_out, register_1_q[1], register_1_q[0], not_1_out);
  and and_4 (and_4_out, not_4_out, not_5_out, req);
  and and_5 (and_5_out, not_4_out, register_1_q[0], not_2_out);
  and and_6 (and_6_out, register_1_q[1], not_5_out, p7s);
  and and_7 (and_7_out, register_1_q[1], register_1_q[0], not_1_out);
  or N1 (N0_out[1], and_1_out, and_2_out, and_3_out);
  or N0 (N0_out[0], and_4_out, and_5_out, and_6_out, and_7_out);
  not not_6 (not_6_out, register_1_q[1]);
  not not_7 (not_7_out, register_1_q[0]);
  and and_8 (and_8_out, not_6_out, not_7_out);
  and and_9 (and_9_out, not_6_out, register_1_q[0]);
  and and_10 (orange, register_1_q[1], not_7_out);
  and and_11 (green, register_1_q[1], register_1_q[0]);
  and and_12 (resetT, not_6_out, not_7_out);
  or or_1 (red, and_8_out, and_9_out);
endmodule
