// Logisim project lab5_main.circ as structural Verilog: 1 circuit, main circuit main
module main (
  input  resetT_and_req,
  input  [6:0] _3,
  input  [6:0] _7,
  input  [6:0] _37
);

  wire clock_1_out, main_1_p3s, main_1_p7s, main_1_p37s, main_2_green, main_2_orange, main_2_red,
       main_2_resett;

  Clock clock_1 (.out(clock_1_out));
  lab5_datapath_main main_1 (
    .resetT(resetT_and_req), .clock(clock_1_out), ._3(_3), ._7(_7), ._37(_37), .p3s(main_1_p3s),
    .p7s(main_1_p7s), .p37s(main_1_p37s));
  lab5_fsm_main main_2 (
    .p3s(main_1_p3s), .p7s(main_1_p7s), .p37s(main_1_p37s), .req(resetT_and_req), .clock(clock_1_out),
    .red(main_2_red), .orange(main_2_orange), .green(main_2_green), .resetT(main_2_resett));
  LED red (.in(main_2_red));
  LED orange (.in(main_2_orange));
  LED green (.in(main_2_green));
  LED resetT (.in(main_2_resett));
endmodule
