// Logisim project datapath.circ as structural Verilog: 1 circuit, main circuit main
module main (
  input  [7:0] _0_constant,
  input  sdiff,
  input  [7:0] xi,
  input  lxi,
  input  ldiff,
  input  ldiff2,
  input  [7:0] yi,
  input  lyi,
  input  [7:0] _1_constant,
  input  [7:0] z,
  input  lzi,
  input  sz,
  input  lresult,
  input  clock,
  output gre,
  output eq,
  output [7:0] result
);

  wire [7:0] diff2_q, diff_q, multiplexer_1_out, multiplexer_2_out, multiplier_1_out, subtractor_1_out,
       subtractor_2_out, x_q, y_q, z_q;

  Multiplexer #(.width(8), .enable("false")) multiplexer_1 (
    .in0(z), .in1(multiplier_1_out), .out(multiplexer_1_out), .sel(sz));
  Register x (.D(xi), .en(lxi), .Q(x_q), .clk(clock));  // open: clr
  Register y (.D(yi), .en(lyi), .Q(y_q), .clk(clock));  // open: clr
  Register u_z (.D(multiplexer_1_out), .en(lzi), .Q(z_q), .clk(clock));  // open: clr
  Subtractor subtractor_1 (.a(x_q), .b(y_q), .out(subtractor_1_out), .bin(1'b0));  // open: bout
  Multiplexer #(.width(8), .enable("false")) multiplexer_2 (
    .in0(subtractor_1_out), .in1(subtractor_2_out), .out(multiplexer_2_out), .sel(sdiff));
  Register diff (.D(multiplexer_2_out), .en(ldiff), .Q(diff_q), .clk(clock));  // open: clr
  Subtractor subtractor_2 (.a(diff_q), .b(_1_constant), .out(subtractor_2_out), .bin(1'b0));  // open: bout
  Register diff2 (.D(diff_q), .en(ldiff2), .Q(diff2_q), .clk(clock));  // open: clr
  Comparator comparator_1 (.a(diff_q), .b(_0_constant), .gt(gre), .eq(eq));  // open: lt
  Multiplier multiplier_1 (.a(diff2_q), .b(z_q), .out(multiplier_1_out));  // open: cin, cout
  Register u_result (.D(z_q), .en(lresult), .Q(result), .clk(clock));  // open: clr
endmodule
