// Logisim project fsm.circ as structural Verilog: 1 circuit, main circuit main
module main (
  input  go,
  input  eq,
  input  gre,
  input  clock,
  output lxi,
  output lyi,
  output lzi,
  output ldiff,
  output ldiff2,
  output sz,
  output sdiff,
  output lresult
);

  wire and_1_out, and_2_out, and_3_out, and_4_out, and_5_out, and_6_out, and_7_out, and_10_out, not_1_out,
       not_2_out, not_3_out, not_4_out, not_5_out, not_6_out, or_1_out, xor_1_out, xor_2_out;
  wire [2:0] N0_out, register_1_q;

  or or_1 (or_1_out, eq, gre);
  Register #(.width(3)) register_1 (.D(N0_out), .Q(register_1_q), .clk(clock));  // open: en, clr
  not not_1 (not_1_out, register_1_q[0]);
  not not_2 (not_2_out, register_1_q[2]);
  not not_3 (not_3_out, register_1_q[1]);
  xor xor_1 (xor_1_out, register_1_q[2], register_1_q[1]);
  and and_1 (and_1_out, xor_1_out, register_1_q[0]);
  and and_2 (and_2_out, register_1_q[2], or_1_out, not_3_out, not_1_out);
  xor xor_2 (xor_2_out, register_1_q[1], register_1_q[0]);
  and and_3 (and_3_out, xor_2_out, not_2_out);
  and and_4 (and_4_out, not_1_out, eq, not_3_out, register_1_q[2]);
  and and_5 (and_5_out, not_2_out, not_3_out, not_1_out, go);
  and and_6 (and_6_out, register_1_q[2], not_3_out, not_1_out, gre);
  and and_7 (and_7_out, not_2_out, register_1_q[1], not_1_out);
  or N2 (N0_out[2], and_1_out, and_2_out);
  or N1 (N0_out[1], and_3_out, and_4_out);
  or N0 (N0_out[0], and_5_out, and_6_out, and_7_out);
  not not_4 (not_4_out, register_1_q[0]);
  not not_5 (not_5_out, register_1_q[1]);
  not not_6 (not_6_out, register_1_q[2]);
  and and_8 (lxi, not_6_out, not_5_out, register_1_q[0]);
  and and_9 (sdiff, register_1_q[2], not_5_out, register_1_q[0]);
  and and_10 (and_10_out, not_6_out, register_1_q[1], not_4_out);
  and and_11 (ldiff2, not_6_out, register_1_q[1], register_1_q[0]);
  and and_12 (lresult, register_1_q[2], register_1_q[1], not_4_out);
  or or_2 (lzi, lxi, sdiff);
  or or_3 (ldiff, sdiff, and_10_out);

  assign lyi = lxi;
  assign sz = sdiff;
endmodule
