// Logisim project main.circ as structural Verilog: 1 circuit, main circuit main
module main (
  input  [7:0] xi,
  input  [7:0] _0,
  input  [7:0] _1,
  input  [7:0] yi,
  input  go,
  output [7:0] result
);

  wire clock_1_out, main_1_ldiff, main_1_ldiff2, main_1_lresult, main_1_lxi, main_1_lyi, main_1_lzi,
       main_1_sdiff, main_1_sz, main_2_eq, main_2_gre;

  Clock clock_1 (.out(clock_1_out));
  fsm_main main_1 (
    .go(go), .eq(main_2_eq), .gre(main_2_gre), .clock(clock_1_out), .lxi(main_1_lxi), .lyi(main_1_lyi),
    .lzi(main_1_lzi), .ldiff(main_1_ldiff), .ldiff2(main_1_ldiff2), .sz(main_1_sz), .sdiff(main_1_sdiff),
    .lresult(main_1_lresult));
  datapath_main main_2 (
    ._0_constant(_0), .xi(xi), .yi(yi), ._1_constant(_1), .z(_1), .sdiff(main_1_sdiff), .clock(clock_1_out),
    .sz(main_1_sz), .lxi(main_1_lxi), .lyi(main_1_lyi), .lzi(main_1_lzi), .ldiff(main_1_ldiff),
    .ldiff2(main_1_ldiff2), .eq(main_2_eq), .gre(main_2_gre), .lresult(main_1_lresult), .result(result));
endmodule
